// Logisim project Unsigned_Divider.circ as structural Verilog: 4 circuits, main circuit FS
module FS (
  input  A,
  input  B,
  input  Bin,
  output D,
  output Bout
);

  wire and_1_out, and_2_out, and_3_out, not_1_out, not_2_out, or_1_out, xor_1_out;

  xor xor_1 (xor_1_out, A, B);
  not not_1 (not_1_out, A);
  and and_1 (and_1_out, not_1_out, Bin);
  not not_2 (not_2_out, A);
  and and_2 (and_2_out, not_2_out, B);
  xor xor_2 (D, xor_1_out, Bin);
  or or_1 (or_1_out, and_1_out, and_2_out);
  and and_3 (and_3_out, B, Bin);
  or or_2 (Bout, or_1_out, and_3_out);
endmodule

module Cell_D (
  input  A,
  input  B,
  input  Bin,
  input  Sel,
  output Bout,
  output Sel_copy,
  output A_D,
  output B_copy
);

  wire fs_1_d;

  FS fs_1 (.A(A), .B(B), .Bin(Bin), .D(fs_1_d), .Bout(Bout));
  Multiplexer #(.enable("false")) multiplexer_1 (.in0(fs_1_d), .in1(A), .out(A_D), .sel(Sel));

  assign B_copy = B;
  assign Sel_copy = Sel;
endmodule

// A0
module _2_bit_Unsigned_Divider (
  input  A1,
  input  A0,
  input  B1,
  input  B0,
  output Q1,
  output Q0,
  output R1,
  output R0,
  output Exception
);

  wire cell_d_1_b_copy, cell_d_1_bout, cell_d_1_sel_copy, cell_d_2_a_d, cell_d_2_b_copy, cell_d_2_bout,
       cell_d_3_bout, cell_d_3_sel_copy, cell_d_4_bout;

  not not_1 (Q1, cell_d_1_bout);
  not not_2 (Q0, cell_d_3_bout);
  Cell_D cell_d_1 (
    .Bout(cell_d_1_bout), .Sel(cell_d_1_bout), .Bin(cell_d_2_bout), .A(1'b0), .B(B1),
    .Sel_copy(cell_d_1_sel_copy), .B_copy(cell_d_1_b_copy));  // open: A_D
  Cell_D cell_d_2 (
    .Bout(cell_d_2_bout), .Sel(cell_d_1_sel_copy), .Bin(1'b0), .A(A1), .B(B0), .A_D(cell_d_2_a_d),
    .B_copy(cell_d_2_b_copy));  // open: Sel_copy
  Cell_D cell_d_3 (
    .Bout(cell_d_3_bout), .Sel(cell_d_3_bout), .Bin(cell_d_4_bout), .A(cell_d_2_a_d), .B(cell_d_1_b_copy),
    .A_D(R1), .Sel_copy(cell_d_3_sel_copy));  // open: B_copy
  Cell_D cell_d_4 (
    .Bout(cell_d_4_bout), .Sel(cell_d_3_sel_copy), .Bin(1'b0), .A(A0), .B(cell_d_2_b_copy), .A_D(R0));  // open: Sel_copy, B_copy
  nor nor_1 (Exception, B1, B0);
endmodule

module _4_bit_Unsigned_Divider (
  input  A3,
  input  A2,
  input  A1,
  input  A0,
  input  B3,
  input  B2,
  input  B1,
  input  B0,
  output Q3,
  output Q2,
  output Q1,
  output Q0,
  output R3,
  output R2,
  output R1,
  output R0,
  output Exception
);

  wire cell_d_1_b_copy, cell_d_1_bout, cell_d_1_sel_copy, cell_d_2_a_d, cell_d_2_b_copy, cell_d_2_bout,
       cell_d_2_sel_copy, cell_d_3_b_copy, cell_d_3_bout, cell_d_3_sel_copy, cell_d_4_a_d, cell_d_4_b_copy,
       cell_d_4_bout, cell_d_4_sel_copy, cell_d_5_a_d, cell_d_5_b_copy, cell_d_5_bout, cell_d_5_sel_copy,
       cell_d_6_b_copy, cell_d_6_bout, cell_d_6_sel_copy, cell_d_7_a_d, cell_d_7_b_copy, cell_d_7_bout,
       cell_d_8_a_d, cell_d_8_b_copy, cell_d_8_bout, cell_d_8_sel_copy, cell_d_9_a_d, cell_d_9_b_copy,
       cell_d_9_bout, cell_d_9_sel_copy, cell_d_10_bout, cell_d_10_sel_copy, cell_d_11_a_d, cell_d_11_b_copy,
       cell_d_11_bout, cell_d_12_a_d, cell_d_12_b_copy, cell_d_12_bout, cell_d_12_sel_copy, cell_d_13_bout,
       cell_d_13_sel_copy, cell_d_14_a_d, cell_d_14_b_copy, cell_d_14_bout, cell_d_15_bout,
       cell_d_15_sel_copy, cell_d_16_bout;

  not not_1 (Q3, cell_d_1_bout);
  Cell_D cell_d_1 (
    .Bout(cell_d_1_bout), .Sel(cell_d_1_bout), .Bin(cell_d_2_bout), .A(1'b0), .B(B3),
    .Sel_copy(cell_d_1_sel_copy), .B_copy(cell_d_1_b_copy));  // open: A_D
  not not_2 (Q2, cell_d_3_bout);
  Cell_D cell_d_2 (
    .Bout(cell_d_2_bout), .Sel(cell_d_1_sel_copy), .Bin(cell_d_4_bout), .A(1'b0), .B(B2), .A_D(cell_d_2_a_d),
    .Sel_copy(cell_d_2_sel_copy), .B_copy(cell_d_2_b_copy));
  Cell_D cell_d_3 (
    .Bout(cell_d_3_bout), .Sel(cell_d_3_bout), .Bin(cell_d_5_bout), .A(cell_d_2_a_d), .B(cell_d_1_b_copy),
    .Sel_copy(cell_d_3_sel_copy), .B_copy(cell_d_3_b_copy));  // open: A_D
  not not_3 (Q1, cell_d_6_bout);
  not not_4 (Q0, cell_d_10_bout);
  Cell_D cell_d_4 (
    .Bout(cell_d_4_bout), .Sel(cell_d_2_sel_copy), .Bin(cell_d_7_bout), .A(1'b0), .B(B1), .A_D(cell_d_4_a_d),
    .Sel_copy(cell_d_4_sel_copy), .B_copy(cell_d_4_b_copy));
  Cell_D cell_d_5 (
    .Bout(cell_d_5_bout), .Sel(cell_d_3_sel_copy), .Bin(cell_d_8_bout), .A(cell_d_4_a_d),
    .B(cell_d_2_b_copy), .A_D(cell_d_5_a_d), .Sel_copy(cell_d_5_sel_copy), .B_copy(cell_d_5_b_copy));
  Cell_D cell_d_6 (
    .Bout(cell_d_6_bout), .Sel(cell_d_6_bout), .Bin(cell_d_9_bout), .A(cell_d_5_a_d), .B(cell_d_3_b_copy),
    .Sel_copy(cell_d_6_sel_copy), .B_copy(cell_d_6_b_copy));  // open: A_D
  Cell_D cell_d_7 (
    .Bout(cell_d_7_bout), .Sel(cell_d_4_sel_copy), .Bin(1'b0), .A(A3), .B(B0), .A_D(cell_d_7_a_d),
    .B_copy(cell_d_7_b_copy));  // open: Sel_copy
  Cell_D cell_d_8 (
    .Bout(cell_d_8_bout), .Sel(cell_d_5_sel_copy), .Bin(cell_d_11_bout), .A(cell_d_7_a_d),
    .B(cell_d_4_b_copy), .A_D(cell_d_8_a_d), .Sel_copy(cell_d_8_sel_copy), .B_copy(cell_d_8_b_copy));
  Cell_D cell_d_9 (
    .Bout(cell_d_9_bout), .Sel(cell_d_6_sel_copy), .Bin(cell_d_12_bout), .A(cell_d_8_a_d),
    .B(cell_d_5_b_copy), .A_D(cell_d_9_a_d), .Sel_copy(cell_d_9_sel_copy), .B_copy(cell_d_9_b_copy));
  Cell_D cell_d_10 (
    .Bout(cell_d_10_bout), .Sel(cell_d_10_bout), .Bin(cell_d_13_bout), .A(cell_d_9_a_d), .B(cell_d_6_b_copy),
    .A_D(R3), .Sel_copy(cell_d_10_sel_copy));  // open: B_copy
  Cell_D cell_d_11 (
    .Bout(cell_d_11_bout), .Sel(cell_d_8_sel_copy), .Bin(1'b0), .A(A2), .B(cell_d_7_b_copy),
    .A_D(cell_d_11_a_d), .B_copy(cell_d_11_b_copy));  // open: Sel_copy
  Cell_D cell_d_12 (
    .Bout(cell_d_12_bout), .Sel(cell_d_9_sel_copy), .Bin(cell_d_14_bout), .A(cell_d_11_a_d),
    .B(cell_d_8_b_copy), .A_D(cell_d_12_a_d), .Sel_copy(cell_d_12_sel_copy), .B_copy(cell_d_12_b_copy));
  Cell_D cell_d_13 (
    .Bout(cell_d_13_bout), .Sel(cell_d_10_sel_copy), .Bin(cell_d_15_bout), .A(cell_d_12_a_d),
    .B(cell_d_9_b_copy), .A_D(R2), .Sel_copy(cell_d_13_sel_copy));  // open: B_copy
  Cell_D cell_d_14 (
    .Bout(cell_d_14_bout), .Sel(cell_d_12_sel_copy), .Bin(1'b0), .A(A1), .B(cell_d_11_b_copy),
    .A_D(cell_d_14_a_d), .B_copy(cell_d_14_b_copy));  // open: Sel_copy
  Cell_D cell_d_15 (
    .Bout(cell_d_15_bout), .Sel(cell_d_13_sel_copy), .Bin(cell_d_16_bout), .A(cell_d_14_a_d),
    .B(cell_d_12_b_copy), .A_D(R1), .Sel_copy(cell_d_15_sel_copy));  // open: B_copy
  Cell_D cell_d_16 (
    .Bout(cell_d_16_bout), .Sel(cell_d_15_sel_copy), .Bin(1'b0), .A(A0), .B(cell_d_14_b_copy), .A_D(R0));  // open: Sel_copy, B_copy
  nor nor_1 (Exception, B3, B2, B1, B0);
endmodule
