// Logisim project Unsigned_Multiplier_Library.circ as structural Verilog: 4 circuits, main circuit FA
module FA (
  input  a,
  input  b,
  input  Cin,
  output S,
  output Cout
);

  wire and_1_out, and_2_out, xor_1_out;

  xor xor_1 (xor_1_out, a, b);
  xor xor_2 (S, xor_1_out, Cin);
  and and_1 (and_1_out, Cin, xor_1_out);
  and and_2 (and_2_out, a, b);
  or or_1 (Cout, and_1_out, and_2_out);
endmodule

module Cell_M (
  input  x,
  input  y,
  input  b,
  input  Cin,
  output Cout,
  output x_copy,
  output s
);

  wire and_1_out;

  and and_1 (and_1_out, x, y);
  FA fa_1 (.S(s), .Cout(Cout), .b(b), .Cin(Cin), .a(and_1_out));

  assign x_copy = x;
endmodule

module Two_into_Two_MUL (
  input  X1,
  input  X0,
  input  Y0,
  input  Y1,
  output P3,
  output P2,
  output P1,
  output P0
);

  wire cell_m_2_cout, cell_m_2_s, cell_m_2_x_copy, cell_m_3_cout, cell_m_4_cout, cell_m_4_x_copy;

  Cell_M cell_m_1 (
    .Cout(P3), .x(cell_m_2_x_copy), .Cin(cell_m_3_cout), .y(Y1), .s(P2), .b(cell_m_2_cout));  // open: x_copy
  Cell_M cell_m_2 (
    .Cout(cell_m_2_cout), .x(X1), .Cin(cell_m_4_cout), .y(Y0), .x_copy(cell_m_2_x_copy), .s(cell_m_2_s),
    .b(1'b0));
  Cell_M cell_m_3 (
    .Cout(cell_m_3_cout), .x(cell_m_4_x_copy), .Cin(1'b0), .y(Y1), .s(P1), .b(cell_m_2_s));  // open: x_copy
  Cell_M cell_m_4 (.Cout(cell_m_4_cout), .x(X0), .Cin(1'b0), .y(Y0), .x_copy(cell_m_4_x_copy), .s(P0), .b(1'b0));
endmodule

module Four_into_Four_MUL (
  input  X3,
  input  X2,
  input  X1,
  input  X0,
  input  Y0,
  input  Y1,
  input  Y2,
  input  Y3,
  output P7,
  output P6,
  output P5,
  output P4,
  output P3,
  output P2,
  output P1,
  output P0
);

  wire cell_m_2_cout, cell_m_2_s, cell_m_2_x_copy, cell_m_3_cout, cell_m_4_cout, cell_m_4_s, cell_m_4_x_copy,
       cell_m_5_cout, cell_m_5_s, cell_m_5_x_copy, cell_m_6_cout, cell_m_7_cout, cell_m_7_s, cell_m_7_x_copy,
       cell_m_8_cout, cell_m_8_s, cell_m_8_x_copy, cell_m_9_cout, cell_m_9_s, cell_m_9_x_copy,
       cell_m_10_cout, cell_m_11_cout, cell_m_11_s, cell_m_11_x_copy, cell_m_12_cout, cell_m_12_s,
       cell_m_12_x_copy, cell_m_13_cout, cell_m_13_x_copy, cell_m_14_cout, cell_m_14_s, cell_m_14_x_copy,
       cell_m_15_cout, cell_m_15_x_copy, cell_m_16_cout, cell_m_16_x_copy;

  Cell_M cell_m_1 (
    .Cout(P7), .x(cell_m_2_x_copy), .Cin(cell_m_3_cout), .y(Y3), .s(P6), .b(cell_m_2_cout));  // open: x_copy
  Cell_M cell_m_2 (
    .Cout(cell_m_2_cout), .x(cell_m_4_x_copy), .Cin(cell_m_5_cout), .y(Y2), .x_copy(cell_m_2_x_copy),
    .s(cell_m_2_s), .b(cell_m_4_cout));
  Cell_M cell_m_3 (
    .Cout(cell_m_3_cout), .x(cell_m_5_x_copy), .Cin(cell_m_6_cout), .y(Y3), .s(P5), .b(cell_m_2_s));  // open: x_copy
  Cell_M cell_m_4 (
    .Cout(cell_m_4_cout), .x(cell_m_7_x_copy), .Cin(cell_m_8_cout), .y(Y1), .x_copy(cell_m_4_x_copy),
    .s(cell_m_4_s), .b(cell_m_7_cout));
  Cell_M cell_m_5 (
    .Cout(cell_m_5_cout), .x(cell_m_8_x_copy), .Cin(cell_m_9_cout), .y(Y2), .x_copy(cell_m_5_x_copy),
    .s(cell_m_5_s), .b(cell_m_4_s));
  Cell_M cell_m_6 (
    .Cout(cell_m_6_cout), .x(cell_m_9_x_copy), .Cin(cell_m_10_cout), .y(Y3), .s(P4), .b(cell_m_5_s));  // open: x_copy
  Cell_M cell_m_7 (
    .Cout(cell_m_7_cout), .x(X3), .Cin(cell_m_11_cout), .y(Y0), .x_copy(cell_m_7_x_copy), .s(cell_m_7_s),
    .b(1'b0));
  Cell_M cell_m_8 (
    .Cout(cell_m_8_cout), .x(cell_m_11_x_copy), .Cin(cell_m_12_cout), .y(Y1), .x_copy(cell_m_8_x_copy),
    .s(cell_m_8_s), .b(cell_m_7_s));
  Cell_M cell_m_9 (
    .Cout(cell_m_9_cout), .x(cell_m_12_x_copy), .Cin(cell_m_13_cout), .y(Y2), .x_copy(cell_m_9_x_copy),
    .s(cell_m_9_s), .b(cell_m_8_s));
  Cell_M cell_m_10 (
    .Cout(cell_m_10_cout), .x(cell_m_13_x_copy), .Cin(1'b0), .y(Y3), .s(P3), .b(cell_m_9_s));  // open: x_copy
  Cell_M cell_m_11 (
    .Cout(cell_m_11_cout), .x(X2), .Cin(cell_m_14_cout), .y(Y0), .x_copy(cell_m_11_x_copy), .s(cell_m_11_s),
    .b(1'b0));
  Cell_M cell_m_12 (
    .Cout(cell_m_12_cout), .x(cell_m_14_x_copy), .Cin(cell_m_15_cout), .y(Y1), .x_copy(cell_m_12_x_copy),
    .s(cell_m_12_s), .b(cell_m_11_s));
  Cell_M cell_m_13 (
    .Cout(cell_m_13_cout), .x(cell_m_15_x_copy), .Cin(1'b0), .y(Y2), .x_copy(cell_m_13_x_copy), .s(P2),
    .b(cell_m_12_s));
  Cell_M cell_m_14 (
    .Cout(cell_m_14_cout), .x(X1), .Cin(cell_m_16_cout), .y(Y0), .x_copy(cell_m_14_x_copy), .s(cell_m_14_s),
    .b(1'b0));
  Cell_M cell_m_15 (
    .Cout(cell_m_15_cout), .x(cell_m_16_x_copy), .Cin(1'b0), .y(Y1), .x_copy(cell_m_15_x_copy), .s(P1),
    .b(cell_m_14_s));
  Cell_M cell_m_16 (.Cout(cell_m_16_cout), .x(X0), .Cin(1'b0), .y(Y0), .x_copy(cell_m_16_x_copy), .s(P0), .b(1'b0));
endmodule
