// Logisim project RAM_library.circ as structural Verilog: 8 circuits, main circuit 1x1 Static RAM Cell
module _1x1_Static_RAM_Cell (
  input  Read_Select_1,
  input  Read_Select_2,
  input  Write_Data,
  input  Write_Select,
  input  Clock,
  output Read_Data_1,
  output Read_Data_2
);

  wire d_ff_1_q, multiplexer_1_out;

  Multiplexer #(.enable("false")) multiplexer_1 (
    .in0(d_ff_1_q), .in1(Write_Data), .out(multiplexer_1_out), .sel(Write_Select));
  D_Flip_Flop d_ff_1 (.clk(Clock), .D(multiplexer_1_out), .Q(d_ff_1_q));  // open: Qn, preset, en, reset
  and and_1 (Read_Data_1, Read_Select_1, d_ff_1_q);
  and and_2 (Read_Data_2, Read_Select_2, d_ff_1_q);
endmodule

module _1x3_SRAM (
  input  Read_Select_1,
  input  Read_Select_2,
  input  Write_Select,
  input  [2:0] Write_Data,
  input  Clock,
  output [2:0] Read_Data_1,
  output [2:0] Read_Date_2
);

  _1x1_Static_RAM_Cell u_1x1_static_ram_cell_1 (
    .Read_Data_1(Read_Data_1[0]), .Write_Select(Write_Select), .Read_Data_2(Read_Date_2[0]),
    .Read_Select_2(Read_Select_2), .Write_Data(Write_Data[0]), .Read_Select_1(Read_Select_1), .Clock(Clock));
  _1x1_Static_RAM_Cell u_1x1_static_ram_cell_2 (
    .Read_Data_1(Read_Data_1[1]), .Write_Select(Write_Select), .Read_Data_2(Read_Date_2[1]),
    .Read_Select_2(Read_Select_2), .Write_Data(Write_Data[1]), .Read_Select_1(Read_Select_1), .Clock(Clock));
  _1x1_Static_RAM_Cell u_1x1_static_ram_cell_3 (
    .Read_Data_1(Read_Data_1[2]), .Write_Select(Write_Select), .Read_Data_2(Read_Date_2[2]),
    .Read_Select_2(Read_Select_2), .Write_Data(Write_Data[2]), .Read_Select_1(Read_Select_1), .Clock(Clock));
endmodule

module _1x13_SRAM (
  input  Read_Select_1,
  input  Read_Select_2,
  input  Write_Select,
  input  Clock,
  input  [12:0] Write_Data,
  output [12:0] Read_Data_1__12_0,
  output [12:0] Read_Data_2__12_0
);

  _1x3_SRAM u_1x3_sram_1 (
    .Read_Select_2(Read_Select_2), .Read_Select_1(Read_Select_1), .Write_Data(Write_Data[12:10]),
    .Read_Data_1(Read_Data_1__12_0[12:10]), .Read_Date_2(Read_Data_2__12_0[12:10]),
    .Write_Select(Write_Select), .Clock(Clock));
  _1x3_SRAM u_1x3_sram_2 (
    .Read_Select_2(Read_Select_2), .Read_Select_1(Read_Select_1), .Write_Data(Write_Data[9:7]),
    .Read_Data_1(Read_Data_1__12_0[9:7]), .Read_Date_2(Read_Data_2__12_0[9:7]), .Write_Select(Write_Select),
    .Clock(Clock));
  _1x3_SRAM u_1x3_sram_3 (
    .Read_Select_2(Read_Select_2), .Read_Select_1(Read_Select_1), .Write_Data(Write_Data[6:4]),
    .Read_Data_1(Read_Data_1__12_0[6:4]), .Read_Date_2(Read_Data_2__12_0[6:4]), .Write_Select(Write_Select),
    .Clock(Clock));
  _1x3_SRAM u_1x3_sram_4 (
    .Read_Select_2(Read_Select_2), .Read_Select_1(Read_Select_1), .Write_Data(Write_Data[3:1]),
    .Read_Data_1(Read_Data_1__12_0[3:1]), .Read_Date_2(Read_Data_2__12_0[3:1]), .Write_Select(Write_Select),
    .Clock(Clock));
  _1x1_Static_RAM_Cell u_1x1_static_ram_cell_1 (
    .Read_Data_1(Read_Data_1__12_0[0]), .Write_Select(Write_Select), .Read_Data_2(Read_Data_2__12_0[0]),
    .Read_Select_2(Read_Select_2), .Write_Data(Write_Data[0]), .Read_Select_1(Read_Select_1), .Clock(Clock));

  // Notes on the sheet:
  //   Write_Data: pull=down
endmodule

module _4x13_SRAM (
  input  [12:0] Write_Data__12_0,
  input  Write_Enable,
  input  [1:0] Write_Address__1_0,
  input  Read_Address1_Enable,
  input  [1:0] Read_Address_1__1_0,
  input  Read_Address2_Enable,
  input  [1:0] Read_Address_2__1_0,
  input  Clock,
  output [12:0] Read_Data_1__12_0,
  output [12:0] Read_Data_2__12_0
);

  wire R1_0, R1_1, R1_2, R1_3, R2_0, R2_0_t, R2_1, R2_1_t, R2_2, R2_3, W0, W1, W2, W3;
  wire [12:0] RD1_0, RD1_1, RD1_2, RD1_3, RD2_0, RD2_1, RD2_2, RD2_3;

  Decoder #(.select(2), .disabled(0)) decoder_1 (
    .out0(W0), .out1(W1), .out2(W2), .out3(W3), .sel(Write_Address__1_0), .en(Write_Enable));
  Decoder #(.select(2), .disabled(0)) decoder_2 (
    .out0(R1_0), .out1(R1_1), .out2(R1_2), .out3(R1_3), .sel(Read_Address_1__1_0), .en(Read_Address1_Enable));
  Decoder #(.select(2), .disabled(0)) decoder_3 (
    .out0(R2_0_t), .out1(R2_1_t), .out2(R2_2), .out3(R2_3), .sel(Read_Address_2__1_0),
    .en(Read_Address2_Enable));
  _1x13_SRAM u_1x13_sram_1 (
    .Read_Select_2(R2_0), .Read_Select_1(R1_0), .Write_Select(W0), .Write_Data(Write_Data__12_0),
    .Read_Data_1__12_0(RD1_0), .Read_Data_2__12_0(RD2_0), .Clock(Clock));
  _1x13_SRAM u_1x13_sram_2 (
    .Read_Select_2(R2_1), .Read_Select_1(R1_1), .Write_Select(W1), .Write_Data(Write_Data__12_0),
    .Read_Data_1__12_0(RD1_1), .Read_Data_2__12_0(RD2_1), .Clock(Clock));
  _1x13_SRAM u_1x13_sram_3 (
    .Read_Select_2(R2_2), .Read_Select_1(R1_2), .Write_Select(W2), .Write_Data(Write_Data__12_0),
    .Read_Data_1__12_0(RD1_2), .Read_Data_2__12_0(RD2_2), .Clock(Clock));
  _1x13_SRAM u_1x13_sram_4 (
    .Read_Select_2(R2_3), .Read_Select_1(R1_3), .Write_Select(W3), .Write_Data(Write_Data__12_0),
    .Read_Data_1__12_0(RD1_3), .Read_Data_2__12_0(RD2_3), .Clock(Clock));
  assign Read_Data_1__12_0 = RD1_0 | RD1_1 | RD1_2 | RD1_3;  // OR_Gate or_1, 13 bits wide
  assign Read_Data_2__12_0 = RD2_0 | RD2_1 | RD2_2 | RD2_3;  // OR_Gate or_2, 13 bits wide
endmodule

module _16x13_SRAM (
  input  [3:0] Read_Address_1__3_0,
  input  [3:0] Read_Address_2__3_0,
  input  Read_Address1_Enable,
  input  Read_Address2_Enable,
  input  [3:0] Write_Address__3_0,
  input  [12:0] Write_Data__12_0,
  input  Write_Enable,
  input  Clock,
  output [12:0] Read_Data_1__12_0,
  output [12:0] Read_Data_2__12_0
);

  wire R1_0, R1_1, R1_2, R1_3, R2_0, R2_0_t, R2_1, R2_1_t, R2_2, R2_3, W0, W1, W2, W3;
  wire [12:0] RD1_0, RD1_1, RD1_2, RD1_3, RD2_0, RD2_1, RD2_2, RD2_3;

  Decoder #(.select(2), .disabled(0)) decoder_1 (
    .out0(R1_0), .out1(R1_1), .out2(R1_2), .out3(R1_3), .sel(Read_Address_1__3_0[3:2]),
    .en(Read_Address1_Enable));
  Decoder #(.select(2), .disabled(0)) decoder_2 (
    .out0(R2_0_t), .out1(R2_1_t), .out2(R2_2), .out3(R2_3), .sel(Read_Address_2__3_0[3:2]),
    .en(Read_Address2_Enable));
  Decoder #(.select(2), .disabled(0)) decoder_3 (
    .out0(W0), .out1(W1), .out2(W2), .out3(W3), .sel(Write_Address__3_0[3:2]), .en(Write_Enable));
  _4x13_SRAM u_4x13_sram_1 (
    .Write_Data__12_0(Write_Data__12_0), .Write_Enable(W0), .Write_Address__1_0(Write_Address__3_0[1:0]),
    .Read_Address_1__1_0(Read_Address_1__3_0[1:0]), .Read_Address_2__1_0(Read_Address_2__3_0[1:0]),
    .Read_Data_1__12_0(RD1_0), .Read_Data_2__12_0(RD2_0), .Clock(Clock), .Read_Address1_Enable(R1_0),
    .Read_Address2_Enable(R2_0));
  _4x13_SRAM u_4x13_sram_2 (
    .Write_Data__12_0(Write_Data__12_0), .Write_Enable(W1), .Write_Address__1_0(Write_Address__3_0[1:0]),
    .Read_Address_1__1_0(Read_Address_1__3_0[1:0]), .Read_Address_2__1_0(Read_Address_2__3_0[1:0]),
    .Read_Data_1__12_0(RD1_1), .Read_Data_2__12_0(RD2_1), .Clock(Clock), .Read_Address1_Enable(R1_1),
    .Read_Address2_Enable(R2_1));
  _4x13_SRAM u_4x13_sram_3 (
    .Write_Data__12_0(Write_Data__12_0), .Write_Enable(W2), .Write_Address__1_0(Write_Address__3_0[1:0]),
    .Read_Address_1__1_0(Read_Address_1__3_0[1:0]), .Read_Address_2__1_0(Read_Address_2__3_0[1:0]),
    .Read_Data_1__12_0(RD1_2), .Read_Data_2__12_0(RD2_2), .Clock(Clock), .Read_Address1_Enable(R1_2),
    .Read_Address2_Enable(R2_2));
  _4x13_SRAM u_4x13_sram_4 (
    .Write_Data__12_0(Write_Data__12_0), .Write_Enable(W3), .Write_Address__1_0(Write_Address__3_0[1:0]),
    .Read_Address_1__1_0(Read_Address_1__3_0[1:0]), .Read_Address_2__1_0(Read_Address_2__3_0[1:0]),
    .Read_Data_1__12_0(RD1_3), .Read_Data_2__12_0(RD2_3), .Clock(Clock), .Read_Address1_Enable(R1_3),
    .Read_Address2_Enable(R2_3));
  assign Read_Data_1__12_0 = RD1_0 | RD1_1 | RD1_2 | RD1_3;  // OR_Gate or_1, 13 bits wide
  assign Read_Data_2__12_0 = RD2_0 | RD2_1 | RD2_2 | RD2_3;  // OR_Gate or_2, 13 bits wide

  // Other names for the same wires on the sheet: RA1_E = Read_Address1_Enable; RA2_E = Read_Address2_Enable;
  //   RA1_0[1:0] = Read_Address_1__3_0[1:0]; RA1_1[1:0] = Read_Address_1__3_0[3:2];
  //   RA2_0[1:0] = Read_Address_2__3_0[1:0]; RA2_1[1:0] = Read_Address_2__3_0[3:2]; WD[12:0] = Write_Data__12_0;
  //   WE = Write_Enable; WA0[1:0] = Write_Address__3_0[1:0]; WA1[1:0] = Write_Address__3_0[3:2]
endmodule

module _64x13_SRAM (
  input  [5:0] Read_Address_1__5_0,
  input  [5:0] Read_Address_2__5_0,
  input  Read_Address1_Enable,
  input  Read_Address2_Enable,
  input  [5:0] Write_Address__5_0,
  input  [12:0] Write_Data__12_0,
  input  Write_Enable,
  input  Clock,
  output [12:0] Read_Data_1__12_0,
  output [12:0] Read_Data_2__12_0
);

  wire R1_0, R1_1, R1_2, R1_3, R2_0, R2_0_t, R2_1, R2_1_t, R2_2, R2_3, W0, W1, W2, W3;
  wire [12:0] RD1_0, RD1_1, RD1_2, RD1_3, RD2_0, RD2_1, RD2_2, RD2_3;

  Decoder #(.select(2), .disabled(0)) decoder_1 (
    .out0(R1_0), .out1(R1_1), .out2(R1_2), .out3(R1_3), .sel(Read_Address_1__5_0[5:4]),
    .en(Read_Address1_Enable));
  Decoder #(.select(2), .disabled(0)) decoder_2 (
    .out0(R2_0_t), .out1(R2_1_t), .out2(R2_2), .out3(R2_3), .sel(Read_Address_2__5_0[5:4]),
    .en(Read_Address2_Enable));
  Decoder #(.select(2), .disabled(0)) decoder_3 (
    .out0(W0), .out1(W1), .out2(W2), .out3(W3), .sel(Write_Address__5_0[5:4]), .en(Write_Enable));
  _16x13_SRAM u_16x13_sram_1 (
    .Write_Data__12_0(Write_Data__12_0), .Write_Enable(W0), .Read_Address1_Enable(R1_0),
    .Read_Address2_Enable(R2_0), .Write_Address__3_0(Write_Address__5_0[3:0]),
    .Read_Address_1__3_0(Read_Address_1__5_0[3:0]), .Read_Address_2__3_0(Read_Address_2__5_0[3:0]),
    .Read_Data_1__12_0(RD1_0), .Read_Data_2__12_0(RD2_0), .Clock(Clock));
  _16x13_SRAM u_16x13_sram_2 (
    .Write_Data__12_0(Write_Data__12_0), .Write_Enable(W1), .Read_Address1_Enable(R1_1),
    .Read_Address2_Enable(R2_1), .Write_Address__3_0(Write_Address__5_0[3:0]),
    .Read_Address_1__3_0(Read_Address_1__5_0[3:0]), .Read_Address_2__3_0(Read_Address_2__5_0[3:0]),
    .Read_Data_1__12_0(RD1_1), .Read_Data_2__12_0(RD2_1), .Clock(Clock));
  _16x13_SRAM u_16x13_sram_3 (
    .Write_Data__12_0(Write_Data__12_0), .Write_Enable(W2), .Read_Address1_Enable(R1_2),
    .Read_Address2_Enable(R2_2), .Write_Address__3_0(Write_Address__5_0[3:0]),
    .Read_Address_1__3_0(Read_Address_1__5_0[3:0]), .Read_Address_2__3_0(Read_Address_2__5_0[3:0]),
    .Read_Data_1__12_0(RD1_2), .Read_Data_2__12_0(RD2_2), .Clock(Clock));
  _16x13_SRAM u_16x13_sram_4 (
    .Write_Data__12_0(Write_Data__12_0), .Write_Enable(W3), .Read_Address1_Enable(R1_3),
    .Read_Address2_Enable(R2_3), .Write_Address__3_0(Write_Address__5_0[3:0]),
    .Read_Address_1__3_0(Read_Address_1__5_0[3:0]), .Read_Address_2__3_0(Read_Address_2__5_0[3:0]),
    .Read_Data_1__12_0(RD1_3), .Read_Data_2__12_0(RD2_3), .Clock(Clock));
  assign Read_Data_1__12_0 = RD1_0 | RD1_1 | RD1_2 | RD1_3;  // OR_Gate or_1, 13 bits wide
  assign Read_Data_2__12_0 = RD2_0 | RD2_1 | RD2_2 | RD2_3;  // OR_Gate or_2, 13 bits wide

  // Other names for the same wires on the sheet: RA1_E = Read_Address1_Enable; RA2_E = Read_Address2_Enable;
  //   RA1_0[3:0] = Read_Address_1__5_0[3:0]; RA1_1[1:0] = Read_Address_1__5_0[5:4];
  //   RA2_0[3:0] = Read_Address_2__5_0[3:0]; RA2_1[1:0] = Read_Address_2__5_0[5:4]; WD[12:0] = Write_Data__12_0;
  //   WE = Write_Enable; WA0[3:0] = Write_Address__5_0[3:0]; WA1[1:0] = Write_Address__5_0[5:4]
endmodule

module _128X13_SRAM (
  input  [6:0] Read_Address_1__6_0,
  input  [6:0] Read_Address_2__6_0,
  input  [6:0] Write_Address__6_0,
  input  [12:0] Write_Data__12_0,
  input  Write_Enable,
  input  Clock,
  output [12:0] Read_Data_1__12_0,
  output [12:0] Read_Data_2__12_0
);

  wire R1_0, R1_1, R2_0, R2_1, W0, W1;
  wire [12:0] RD1_0, RD1_1, RD2_0, RD2_1;

  Decoder #(.disabled(0), .enable("false")) decoder_1 (.out0(R1_0), .out1(R1_1), .sel(Read_Address_1__6_0[6]));
  Decoder #(.disabled(0), .enable("false")) decoder_2 (.out0(R2_0), .out1(R2_1), .sel(Read_Address_2__6_0[6]));
  Decoder #(.disabled(0)) decoder_3 (.out0(W0), .out1(W1), .sel(Write_Address__6_0[6]), .en(Write_Enable));
  _64x13_SRAM u_64x13_sram_1 (
    .Read_Address_1__5_0(Read_Address_1__6_0[5:0]), .Read_Address_2__5_0(Read_Address_2__6_0[5:0]),
    .Write_Address__5_0(Write_Address__6_0[5:0]), .Write_Data__12_0(Write_Data__12_0), .Write_Enable(W0),
    .Clock(Clock), .Read_Data_1__12_0(RD1_0), .Read_Data_2__12_0(RD2_0), .Read_Address1_Enable(R1_0),
    .Read_Address2_Enable(R2_0));
  _64x13_SRAM u_64x13_sram_2 (
    .Read_Address_1__5_0(Read_Address_1__6_0[5:0]), .Read_Address_2__5_0(Read_Address_2__6_0[5:0]),
    .Write_Address__5_0(Write_Address__6_0[5:0]), .Write_Data__12_0(Write_Data__12_0), .Write_Enable(W1),
    .Clock(Clock), .Read_Data_1__12_0(RD1_1), .Read_Data_2__12_0(RD2_1), .Read_Address1_Enable(R1_1),
    .Read_Address2_Enable(R2_1));
  assign Read_Data_1__12_0 = RD1_0 | RD1_1;  // OR_Gate or_1, 13 bits wide
  assign Read_Data_2__12_0 = RD2_0 | RD2_1;  // OR_Gate or_2, 13 bits wide

  // Other names for the same wires on the sheet: RA1_0[5:0] = Read_Address_1__6_0[5:0];
  //   RA1_1 = Read_Address_1__6_0[6]; RA2_0[5:0] = Read_Address_2__6_0[5:0]; RA2_1 = Read_Address_2__6_0[6];
  //   WD[12:0] = Write_Data__12_0; WE = Write_Enable; WA0[5:0] = Write_Address__6_0[5:0]; WA1 = Write_Address__6_0[6]
endmodule

module RAM_Testing (
  input  [6:0] Read_Address_1__6_0,
  input  [6:0] Read_Address_2__6_0,
  input  [6:0] Write_Address__6_0,
  input  [12:0] Write_Data__12_0,
  input  Write_Enable,
  input  Clock,
  output [12:0] Read_Data_1__12_0,
  output [12:0] Read_Data_2__12_0
);

  _128X13_SRAM u_128x13_sram_1 (
    .Read_Address_1__6_0(Read_Address_1__6_0), .Read_Address_2__6_0(Read_Address_2__6_0),
    .Write_Address__6_0(Write_Address__6_0), .Write_Data__12_0(Write_Data__12_0),
    .Write_Enable(Write_Enable), .Clock(Clock), .Read_Data_1__12_0(Read_Data_1__12_0),
    .Read_Data_2__12_0(Read_Data_2__12_0));
endmodule
