// Logisim project CPU_Library (Upto LOAD _ STORE).circ as structural Verilog: 5 circuits, main circuit 7-bit Counter
module _7_bit_Counter (
  input  [6:0] I__6_0,
  input  Clock,
  output [6:0] O__6_0
);

  D_Flip_Flop d_ff_1 (.clk(Clock), .D(I__6_0[6]), .Q(O__6_0[6]));  // open: Qn, preset, en, reset
  D_Flip_Flop d_ff_2 (.clk(Clock), .D(I__6_0[5]), .Q(O__6_0[5]));  // open: Qn, preset, en, reset
  D_Flip_Flop d_ff_3 (.clk(Clock), .D(I__6_0[4]), .Q(O__6_0[4]));  // open: Qn, preset, en, reset
  D_Flip_Flop d_ff_4 (.clk(Clock), .D(I__6_0[3]), .Q(O__6_0[3]));  // open: Qn, preset, en, reset
  D_Flip_Flop d_ff_5 (.clk(Clock), .D(I__6_0[2]), .Q(O__6_0[2]));  // open: Qn, preset, en, reset
  D_Flip_Flop d_ff_6 (.clk(Clock), .D(I__6_0[1]), .Q(O__6_0[1]));  // open: Qn, preset, en, reset
  D_Flip_Flop d_ff_7 (.clk(Clock), .D(I__6_0[0]), .Q(O__6_0[0]));  // open: Qn, preset, en, reset
endmodule

module ROM (
  input  Clock,
  input  PC_Enable,
  output [6:0] Physical_Address,
  output [12:0] Data,
  output Write_Enable,
  output PC_Clock
);

  wire [3:1] rom_1_data;

  Counter #(.width(7), .max('h7f), .ongoal("stay")) counter_1 (
    .Q(Physical_Address), .clk(Clock));  // open: load, D, count, carry, clr
  not not_1 (Write_Enable, PC_Enable);
  and and_1 (PC_Clock, Clock, PC_Enable);
  ROM_part #(.addrWidth(7), .dataWidth(16)) rom_1 (
    .addr(Physical_Address), .data({Data[12:1], rom_1_data, Data[0]}));  // open: sel

  // Notes on the sheet:
  //   contents of rom_1 (hex, n*v repeats v):
  //   8*0 a40 9b0 5621 55b0 ce00 cd81 800 890 c000 c081 2c10 8ca1 80b1 5410 cc00 80b1
endmodule

module Control_Unit (
  input  [5:0] Opcode_5_0,
  input  ZF,
  input  SF,
  input  CF,
  output Imm_Sel,
  output REG_EN,
  output [3:0] Op_3_0,
  output RAM_EN,
  output [1:0] ST_Sel,
  output LD_EN,
  output [1:0] LD_Sel,
  output Jmp_Reg_Sel,
  output Jmp_Sel
);

  wire and_1_out, and_2_out, and_3_out, and_4_out, and_5_out, and_6_out, CMP_out, Imm_2_out, JC_out, JE_out,
       JG_out, JGE_out, JL_out, JLE_out, Jmp_2_out, Jmp_3_out, JMP_out, JMP_REG_out, JNC_out, JNE_out,
       JNZ_out, JZ_out, LD_Dir_out, LD_RIn_out, Mem_out, not_1_out, not_2_out, not_3_out, or_1_out, or_2_out,
       or_3_out, or_5_out, or_7_out, Reg_out, ST_Dir_out, ST_Rin_out;

  and Mem (Mem_out, Opcode_5_0[5], Opcode_5_0[4]);
  and LD_Dir (LD_Dir_out, ~Opcode_5_0[0], ~Opcode_5_0[1], ~Opcode_5_0[2], ~Opcode_5_0[3]);  // AND_Gate
  and and_1 (and_1_out, LD_Dir_out, Mem_out);
  and JMP (JMP_out, ~Opcode_5_0[0], ~Opcode_5_0[1], ~Opcode_5_0[2], ~Opcode_5_0[3]);  // AND_Gate
  and Imm (Imm_Sel, ~Opcode_5_0[5], Opcode_5_0[4]);  // AND_Gate
  and Jmp_2 (Jmp_2_out, Opcode_5_0[5], ~Opcode_5_0[4]);  // AND_Gate
  and Imm_2 (Imm_2_out, ~Opcode_5_0[5], Opcode_5_0[4]);  // AND_Gate
  and Reg (Reg_out, ~Opcode_5_0[5], ~Opcode_5_0[4]);  // AND_Gate
  not not_1 (not_1_out, Opcode_5_0[2]);
  and LD_RIn (LD_RIn_out, Opcode_5_0[0], ~Opcode_5_0[1], ~Opcode_5_0[2], ~Opcode_5_0[3]);  // AND_Gate
  and and_2 (and_2_out, LD_RIn_out, Mem_out);
  and JE (JE_out, ~SF, ZF, Opcode_5_0[0], ~Opcode_5_0[1], ~Opcode_5_0[2], ~Opcode_5_0[3]);  // AND_Gate
  and CMP (CMP_out, Opcode_5_0[3], not_1_out, Opcode_5_0[1], Opcode_5_0[0]);
  and ST_Dir (ST_Dir_out, Opcode_5_0[0], Opcode_5_0[1], ~Opcode_5_0[2], ~Opcode_5_0[3]);  // AND_Gate
  and and_3 (and_3_out, ST_Dir_out, Mem_out);
  and JNE (JNE_out, ~ZF, ~Opcode_5_0[0], Opcode_5_0[1], ~Opcode_5_0[2], ~Opcode_5_0[3]);  // AND_Gate
  and Jmp_3 (Jmp_3_out, Opcode_5_0[5], ~Opcode_5_0[4]);  // AND_Gate
  or or_1 (or_1_out, Imm_2_out, Reg_out);
  and and_4 (and_4_out, or_1_out, CMP_out);
  and ST_Rin (ST_Rin_out, ~Opcode_5_0[0], ~Opcode_5_0[1], Opcode_5_0[2], ~Opcode_5_0[3]);  // AND_Gate
  and and_5 (and_5_out, ST_Rin_out, Mem_out);
  and JL (JL_out, SF, ~ZF, Opcode_5_0[0], Opcode_5_0[1], ~Opcode_5_0[2], ~Opcode_5_0[3]);  // AND_Gate
  or or_2 (or_2_out, SF, ZF);
  and JLE (JLE_out, or_2_out, ~Opcode_5_0[0], ~Opcode_5_0[1], Opcode_5_0[2], ~Opcode_5_0[3]);  // AND_Gate
  and JG (JG_out, ~SF, ~ZF, Opcode_5_0[0], ~Opcode_5_0[1], Opcode_5_0[2], ~Opcode_5_0[3]);  // AND_Gate
  or or_3 (or_3_out, JMP_out, JE_out, JNE_out, JL_out, JLE_out, JG_out, JGE_out, JC_out, JNC_out, JZ_out, JNZ_out);
  or or_4 (RAM_EN, and_3_out, and_5_out);
  not not_2 (not_2_out, RAM_EN);
  or or_5 (or_5_out, ~SF, ZF);  // OR_Gate
  and JGE (JGE_out, or_5_out, ~Opcode_5_0[0], Opcode_5_0[1], Opcode_5_0[2], ~Opcode_5_0[3]);  // AND_Gate
  or or_6 (LD_EN, and_1_out, and_2_out);
  and JC (JC_out, CF, Opcode_5_0[0], Opcode_5_0[1], Opcode_5_0[2], ~Opcode_5_0[3]);  // AND_Gate
  Priority_Encoder #(.select(2), .disabled(0)) priority_encoder_1 (
    .in0(not_2_out), .in1(and_3_out), .in2(and_5_out), .out(ST_Sel));  // open: in3, gs, en_out, en_in
  not not_3 (not_3_out, LD_EN);
  and JNC (JNC_out, ~CF, ~Opcode_5_0[0], ~Opcode_5_0[1], ~Opcode_5_0[2], Opcode_5_0[3]);  // AND_Gate
  and and_6 (and_6_out, or_3_out, Jmp_3_out);
  and JZ (JZ_out, ZF, Opcode_5_0[0], ~Opcode_5_0[1], ~Opcode_5_0[2], Opcode_5_0[3]);  // AND_Gate
  or or_7 (or_7_out, Jmp_2_out, and_4_out, RAM_EN);
  not not_4 (REG_EN, or_7_out);
  Priority_Encoder #(.select(2), .disabled(0)) priority_encoder_2 (
    .in0(not_3_out), .in1(and_1_out), .in2(and_2_out), .out(LD_Sel));  // open: in3, gs, en_out, en_in
  and JNZ (JNZ_out, ~ZF, ~Opcode_5_0[0], Opcode_5_0[1], ~Opcode_5_0[2], Opcode_5_0[3]);  // AND_Gate
  and JMP_REG (JMP_REG_out, Opcode_5_0[0], Opcode_5_0[1], ~Opcode_5_0[2], Opcode_5_0[3]);  // AND_Gate
  and and_7 (Jmp_Reg_Sel, Jmp_3_out, JMP_REG_out);
  or or_8 (Jmp_Sel, Jmp_Reg_Sel, and_6_out);

  assign Op_3_0 = Opcode_5_0[3:0];
endmodule

module PC_Adder (
  input  [6:0] Input_Address__6_0,
  output [6:0] Output_Address__6_0
);

  wire [6:0] bit_extender_1_out;

  assign bit_extender_1_out = {{6{1'b0}}, 1'b1};  // Bit_Extender bit_extender_1
  Adder #(.width(7)) adder_1 (
    .a(Input_Address__6_0), .b(bit_extender_1_out), .out(Output_Address__6_0), .cin(1'b0));  // open: cout
endmodule

module CPU__Upto_LOAD___STORE (
  input  PC_Enable,
  input  [2:0] LOG_Sel_2_0
);

  wire alu_1_carry_flag, alu_1_sign_flag, alu_1_zero_flag, CF, CLK, CPU_CLK, Imm_Sel, Jmp_Reg_Sel, Jmp_Sel,
       LD_EN, or_1_out, RAM_EN, REG_EN, ROM_WE, SF, ZF;
  wire [1:0] LD_Sel, ST_Sel;
  wire [3:0] alu_1_r__3_0, JMP_ST_Data, LD_Data, multiplexer_6_out, multiplexer_7_out, Op,
       register_set_with_8_8_bit_registers_1_b;
  wire [6:0] LD_ST_Ad, LD_ST_Ad_2, LOG_Address, multiplexer_1_out, multiplexer_4_out,
       pc_adder_1_output_address__6_0, Phy_Address, RAM_RAD, RAM_WAD;
  wire [12:0] bit_extender_1_out, LOG_Ins, multiplexer_2_out, ROM_Date;
  wire [12:4] n128x13_sram_1_read_data_2__12_0;
  wire [25:0] A0, A2, A4, A6, A8, A10, A12, A14;
  wire [31:0] LOG_R;

  Clock Clock (.out(CLK));
  DotMatrix #(.inputtype("row"), .matrixcols(13), .matrixrows(2), .dotshape("circle")) dotmatrix_1 (
    .row0(A0[25:13]), .row1(A0[12:0]));
  DotMatrix #(.inputtype("row"), .matrixcols(13), .matrixrows(2), .dotshape("circle")) dotmatrix_2 (
    .row0(A2[25:13]), .row1(A2[12:0]));
  DotMatrix #(.inputtype("row"), .matrixcols(13), .matrixrows(2), .dotshape("circle")) dotmatrix_3 (
    .row0(A4[25:13]), .row1(A4[12:0]));
  DotMatrix #(.inputtype("row"), .matrixcols(13), .matrixrows(2), .dotshape("circle")) dotmatrix_4 (
    .row0(A6[25:13]), .row1(A6[12:0]));
  DotMatrix #(.inputtype("row"), .matrixcols(13), .matrixrows(2), .dotshape("circle")) dotmatrix_5 (
    .row0(A8[25:13]), .row1(A8[12:0]));
  DotMatrix #(.inputtype("row"), .matrixcols(13), .matrixrows(2), .dotshape("circle")) dotmatrix_6 (
    .row0(A10[25:13]), .row1(A10[12:0]));
  DotMatrix #(.inputtype("row"), .matrixcols(13), .matrixrows(2), .dotshape("circle")) dotmatrix_7 (
    .row0(A12[25:13]), .row1(A12[12:0]));
  DotMatrix #(.inputtype("row"), .matrixcols(13), .matrixrows(2), .dotshape("circle")) dotmatrix_8 (
    .row0(A14[25:13]), .row1(A14[12:0]));
  Multiplexer #(.width(7), .disabled(0), .enable("false")) multiplexer_1 (
    .in0(pc_adder_1_output_address__6_0), .in1(multiplexer_4_out), .out(multiplexer_1_out), .sel(Jmp_Sel));
  ROM rom_1 (
    .Physical_Address(Phy_Address), .Data(ROM_Date), .Clock(CLK), .Write_Enable(ROM_WE),
    .PC_Enable(PC_Enable), .PC_Clock(CPU_CLK));
  PC_Adder pc_adder_1 (.Input_Address__6_0(LOG_Address), .Output_Address__6_0(pc_adder_1_output_address__6_0));
  _7_bit_Counter u_7_bit_counter_1 (.Clock(CPU_CLK), .I__6_0(multiplexer_1_out), .O__6_0(LOG_Address));
  assign bit_extender_1_out = {{9{1'b0}}, JMP_ST_Data};  // Bit_Extender bit_extender_1
  Multiplexer #(.width(13), .enable("false")) multiplexer_2 (
    .in0(bit_extender_1_out), .in1(ROM_Date), .out(multiplexer_2_out), .sel(ROM_WE));
  or or_1 (or_1_out, ROM_WE, RAM_EN);
  Multiplexer #(.select(2), .width(7), .enable("false")) multiplexer_3 (
    .in1(LD_ST_Ad), .in2(LD_ST_Ad_2), .out(RAM_RAD), .sel(LD_Sel));  // open: in0, in3
  DotMatrix #(.inputtype("row"), .matrixcols(7), .matrixrows(1), .dotshape("circle")) dotmatrix_9 (.row0(LOG_Address));
  DotMatrix #(.inputtype("row"), .matrixcols(2), .matrixrows(1), .dotshape("circle")) dotmatrix_10 (.row0(LOG_Ins[12:11]));
  DotMatrix #(.inputtype("row"), .matrixcols(4), .matrixrows(1), .dotshape("circle")) dotmatrix_11 (.row0(LOG_Ins[10:7]));
  DotMatrix #(.inputtype("row"), .matrixcols(3), .matrixrows(1), .dotshape("circle")) dotmatrix_12 (.row0(LOG_Ins[6:4]));
  DotMatrix #(.inputtype("row"), .matrixcols(3), .matrixrows(1), .dotshape("circle")) dotmatrix_13 (.row0(LOG_Ins[3:1]));
  DotMatrix #(.inputtype("row"), .matrixcols(3), .matrixrows(1), .dotshape("circle")) dotmatrix_14 (.row0(LOG_Ins[6:4]));
  DotMatrix #(.inputtype("row"), .matrixcols(4), .matrixrows(1), .dotshape("circle")) dotmatrix_15 (.row0(LOG_Ins[3:0]));
  DotMatrix #(.inputtype("row"), .matrixcols(7), .matrixrows(1), .dotshape("circle")) dotmatrix_16 (.row0(LOG_Ins[6:0]));
  Multiplexer #(.width(7), .disabled(0), .enable("false")) multiplexer_4 (
    .in0(LOG_Ins[6:0]), .in1({3'b000, JMP_ST_Data}), .out(multiplexer_4_out), .sel(Jmp_Reg_Sel));
  _128X13_SRAM u_128x13_sram_1 (
    .Read_Address_1__6_0(LOG_Address), .Read_Address_2__6_0(RAM_RAD), .Write_Address__6_0(RAM_WAD),
    .Write_Data__12_0(multiplexer_2_out), .Write_Enable(or_1_out), .Clock(CLK), .LOG_Sel_2_0(LOG_Sel_2_0),
    ._0(A0), ._2(A2), ._4(A4), ._6(A6), .Read_Data_1__12_0(LOG_Ins), ._8(A8),
    .Read_Data_2__12_0({n128x13_sram_1_read_data_2__12_0, LD_Data}), ._10(A10), ._12(A12), ._14(A14));
  Multiplexer #(.select(2), .width(7), .enable("false")) multiplexer_5 (
    .in0(Phy_Address), .in1(LD_ST_Ad), .in2(LD_ST_Ad_2), .out(RAM_WAD), .sel(ST_Sel));  // open: in3
  DotMatrix #(.inputtype("row"), .matrixcols(4), .matrixrows(1), .dotshape("circle")) dotmatrix_17 (.row0(LOG_R[3:0]));
  DotMatrix #(.inputtype("row"), .matrixcols(4), .matrixrows(1), .dotshape("circle")) dotmatrix_18 (.row0(LOG_R[7:4]));
  DotMatrix #(.inputtype("row"), .matrixcols(4), .matrixrows(1), .dotshape("circle")) dotmatrix_19 (.row0(LOG_R[11:8]));
  DotMatrix #(.inputtype("row"), .matrixcols(4), .matrixrows(1), .dotshape("circle")) dotmatrix_20 (.row0(LOG_R[15:12]));
  DotMatrix #(.inputtype("row"), .matrixcols(4), .matrixrows(1), .dotshape("circle")) dotmatrix_21 (.row0(LOG_R[19:16]));
  DotMatrix #(.inputtype("row"), .matrixcols(4), .matrixrows(1), .dotshape("circle")) dotmatrix_22 (.row0(LOG_R[23:20]));
  DotMatrix #(.inputtype("row"), .matrixcols(4), .matrixrows(1), .dotshape("circle")) dotmatrix_23 (.row0(LOG_R[27:24]));
  DotMatrix #(.inputtype("row"), .matrixcols(4), .matrixrows(1), .dotshape("circle")) dotmatrix_24 (.row0(LOG_R[31:28]));
  Control_Unit control_unit_1 (
    .Opcode_5_0(LOG_Ins[12:7]), .Op_3_0(Op), .Imm_Sel(Imm_Sel), .REG_EN(REG_EN), .LD_Sel(LD_Sel),
    .ST_Sel(ST_Sel), .RAM_EN(RAM_EN), .LD_EN(LD_EN), .ZF(ZF), .SF(SF), .CF(CF), .Jmp_Reg_Sel(Jmp_Reg_Sel),
    .Jmp_Sel(Jmp_Sel));
  Register_Set_with_8_8_bit_Registers register_set_with_8_8_bit_registers_1 (
    .Wr(LOG_Ins[6:4]), .Wrd(multiplexer_7_out), .Clock(CPU_CLK), .Ra(LOG_Ins[6:4]), .Rb(LOG_Ins[3:1]),
    .A(JMP_ST_Data), .B(register_set_with_8_8_bit_registers_1_b), .REG_EN(REG_EN), .LOG_R(LOG_R));  // open: Input_Data, Input_EN, Output_Data
  ALU alu_1 (
    .A__3_0(JMP_ST_Data), .B_3_0(multiplexer_6_out), .OP_3_0(Op), .Carry_Flag(alu_1_carry_flag),
    .R__3_0(alu_1_r__3_0), .Sign_Flag(alu_1_sign_flag), .Zero_Flag(alu_1_zero_flag));  // open: MUL_Excep, DIV_Excep
  FLAG_Register flag_register_1 (
    .CF(alu_1_carry_flag), .SF(alu_1_sign_flag), .ZF(alu_1_zero_flag), .Clock(CPU_CLK), .ZF_2(CF), .SF_2(SF),
    .ZF_3(ZF));
  Multiplexer #(.width(4), .disabled(0), .enable("false")) multiplexer_6 (
    .in0(register_set_with_8_8_bit_registers_1_b), .in1(LOG_Ins[3:0]), .out(multiplexer_6_out), .sel(Imm_Sel));
  assign LD_ST_Ad = {{3{1'b0}}, LOG_Ins[3:0]};  // Bit_Extender bit_extender_2
  assign LD_ST_Ad_2 = {{3{1'b0}}, multiplexer_6_out};  // Bit_Extender bit_extender_3
  Multiplexer #(.width(4), .enable("false")) multiplexer_7 (
    .in0(alu_1_r__3_0), .in1(LD_Data), .out(multiplexer_7_out), .sel(LD_EN));

  // Other names for the same wires on the sheet: Sel[2:0] = LOG_Sel_2_0

  // Notes on the sheet:
  //   A0+A1
  //   A2+A3
  //   A4+A5
  //   A6+A7
  //   A8+A9
  //   A10+A11
  //   A12+A13
  //   A14+A15
  //   Opcode
  //   Ra/Wr
  //   Rb
  //   Ra/Wr
  //   Imm_value
  //   Instruction Address
  //   Instruction Type
  //   Jmp_value
  //   R0
  //   R1
  //   R2
  //   R3
  //   R4
  //   SP
  //   OUTR
  //   INR
endmodule
