// Logisim project Register_Set_Library V2.circ as structural Verilog: 6 circuits, main circuit 1-bit Register
module _1_bit_Register (
  input  Din,
  input  Sel,
  input  Clock,
  output Dout
);

  wire n1_bit_2to1_mux_1_out;

  _1_bit_2to1_MUX u_1_bit_2to1_mux_1 (.A(Dout), .Sel(Sel), .B(Din), .Out(n1_bit_2to1_mux_1_out));
  D_Flip_Flop d_ff_1 (.clk(Clock), .D(n1_bit_2to1_mux_1_out), .Q(Dout));  // open: Qn, preset, en, reset
endmodule

module _1_bit_2to1_MUX (
  input  A,
  input  Sel,
  input  B,
  output Out
);

  wire and_1_out, and_2_out, not_1_out;

  not not_1 (not_1_out, Sel);
  and and_1 (and_1_out, A, not_1_out);
  and and_2 (and_2_out, Sel, B);
  or or_1 (Out, and_1_out, and_2_out);
endmodule

module _8_bit_Register (
  input  [7:0] Din_7_0,
  input  Sel,
  input  Clock,
  output [7:0] Dout_7_0
);

  _1_bit_Register u_1_bit_register_1 (.Din(Din_7_0[7]), .Sel(Sel), .Dout(Dout_7_0[7]), .Clock(Clock));
  _1_bit_Register u_1_bit_register_2 (.Din(Din_7_0[6]), .Sel(Sel), .Dout(Dout_7_0[6]), .Clock(Clock));
  _1_bit_Register u_1_bit_register_3 (.Din(Din_7_0[5]), .Sel(Sel), .Dout(Dout_7_0[5]), .Clock(Clock));
  _1_bit_Register u_1_bit_register_4 (.Din(Din_7_0[4]), .Sel(Sel), .Dout(Dout_7_0[4]), .Clock(Clock));
  _1_bit_Register u_1_bit_register_5 (.Din(Din_7_0[3]), .Sel(Sel), .Dout(Dout_7_0[3]), .Clock(Clock));
  _1_bit_Register u_1_bit_register_6 (.Din(Din_7_0[2]), .Sel(Sel), .Dout(Dout_7_0[2]), .Clock(Clock));
  _1_bit_Register u_1_bit_register_7 (.Din(Din_7_0[1]), .Sel(Sel), .Dout(Dout_7_0[1]), .Clock(Clock));
  _1_bit_Register u_1_bit_register_8 (.Din(Din_7_0[0]), .Sel(Sel), .Dout(Dout_7_0[0]), .Clock(Clock));
endmodule

module _4_bit_Register (
  input  [3:0] Din_3_0,
  input  Sel,
  input  Clock,
  output [3:0] Dout_3_0
);

  _1_bit_Register u_1_bit_register_1 (.Din(Din_3_0[0]), .Sel(Sel), .Dout(Dout_3_0[0]), .Clock(Clock));
  _1_bit_Register u_1_bit_register_2 (.Din(Din_3_0[1]), .Sel(Sel), .Dout(Dout_3_0[1]), .Clock(Clock));
  _1_bit_Register u_1_bit_register_3 (.Din(Din_3_0[2]), .Sel(Sel), .Dout(Dout_3_0[2]), .Clock(Clock));
  _1_bit_Register u_1_bit_register_4 (.Din(Din_3_0[3]), .Sel(Sel), .Dout(Dout_3_0[3]), .Clock(Clock));
endmodule

module Register_Set_with_8_8_bit_Registers (
  input  REG_EN,
  input  [2:0] Wr,
  input  [3:0] Wrd,
  input  [3:0] Input_Data,
  input  Input_EN,
  input  Clock,
  input  [2:0] Ra,
  input  [2:0] Rb,
  output [3:0] A,
  output [3:0] B,
  output [3:0] Output_Data,
  output [31:0] LOG_R
);

  wire Reg0, Reg1, Reg2, Reg3, Reg4, Reg5, Reg6;

  Decoder #(.select(3)) decoder_1 (
    .out0(Reg0), .out1(Reg1), .out2(Reg2), .out3(Reg3), .out4(Reg4), .out5(Reg5), .out6(Reg6), .sel(Wr),
    .en(REG_EN));  // open: out7
  _4_bit_Register Register_0 (.Din_3_0(Wrd), .Sel(Reg0), .Clock(Clock), .Dout_3_0(LOG_R[3:0]));
  _4_bit_Register Register_1 (.Din_3_0(Wrd), .Sel(Reg1), .Clock(Clock), .Dout_3_0(LOG_R[7:4]));
  _4_bit_Register Register_2 (.Din_3_0(Wrd), .Sel(Reg2), .Clock(Clock), .Dout_3_0(LOG_R[11:8]));
  _4_bit_Register Register_3 (.Din_3_0(Wrd), .Sel(Reg3), .Clock(Clock), .Dout_3_0(LOG_R[15:12]));
  _4_bit_Register Register_4 (.Din_3_0(Wrd), .Sel(Reg4), .Clock(Clock), .Dout_3_0(LOG_R[19:16]));
  _4_bit_Register STACK_REGISTER (.Din_3_0(Wrd), .Sel(Reg5), .Clock(Clock), .Dout_3_0(LOG_R[23:20]));
  _4_bit_Register OUTPUT_REGISTER (.Din_3_0(Wrd), .Sel(Reg6), .Clock(Clock), .Dout_3_0(LOG_R[27:24]));
  _4_bit_Register INPUT_REGISTER (.Din_3_0(Input_Data), .Sel(Input_EN), .Clock(Clock), .Dout_3_0(LOG_R[31:28]));
  Multiplexer #(.select(3), .width(4), .enable("false")) multiplexer_1 (
    .in0(LOG_R[3:0]), .in1(LOG_R[7:4]), .in2(LOG_R[11:8]), .in3(LOG_R[15:12]), .in4(LOG_R[19:16]),
    .in5(LOG_R[23:20]), .in6(LOG_R[27:24]), .in7(LOG_R[31:28]), .out(A), .sel(Ra));
  Multiplexer #(.select(3), .width(4), .enable("false")) multiplexer_2 (
    .in0(LOG_R[3:0]), .in1(LOG_R[7:4]), .in2(LOG_R[11:8]), .in3(LOG_R[15:12]), .in4(LOG_R[19:16]),
    .in5(LOG_R[23:20]), .in6(LOG_R[27:24]), .in7(LOG_R[31:28]), .out(B), .sel(Rb));

  assign Output_Data = LOG_R[27:24];

  // Other names for the same wires on the sheet: R0[3:0] = LOG_R[3:0]; R1[3:0] = LOG_R[7:4]; R2[3:0] = LOG_R[11:8];
  //   R3[3:0] = LOG_R[15:12]; R4[3:0] = LOG_R[19:16]; R5[3:0] = LOG_R[23:20]; R6[3:0] = LOG_R[27:24];
  //   R7[3:0] = LOG_R[31:28]
endmodule

module FLAG_Register (
  input  CF,
  input  SF,
  input  ZF,
  input  Clock,
  output ZF_2,
  output SF_2,
  output ZF_3
);

  _1_bit_Register u_1_bit_register_1 (.Din(CF), .Sel(1'b1), .Dout(ZF_2), .Clock(Clock));
  _1_bit_Register u_1_bit_register_2 (.Din(SF), .Sel(1'b1), .Dout(SF_2), .Clock(Clock));
  _1_bit_Register u_1_bit_register_3 (.Din(ZF), .Sel(1'b1), .Dout(ZF_3), .Clock(Clock));
endmodule
