// Logisim project RAM_library V3.circ as structural Verilog: 8 circuits, main circuit 1x1 Static RAM Cell
module _1x1_Static_RAM_Cell (
  input  Read_Select_1,
  input  Read_Select_2,
  input  Write_Select,
  input  Write_Data,
  input  Clock,
  output Read_Data_1,
  output Read_Data_2,
  output LOG_Data
);

  wire and_1_out, and_2_out, not_1_out, or_1_out;

  not not_1 (not_1_out, Write_Select);
  and and_1 (and_1_out, LOG_Data, not_1_out);
  and and_2 (and_2_out, Write_Select, Write_Data);
  D_Flip_Flop d_ff_1 (.clk(Clock), .D(or_1_out), .Q(LOG_Data));  // open: Qn, preset, en, reset
  or or_1 (or_1_out, and_1_out, and_2_out);
  and and_3 (Read_Data_1, Read_Select_1, LOG_Data);
  and and_4 (Read_Data_2, Read_Select_2, LOG_Data);
endmodule

module _1x3_SRAM (
  input  Read_Select_1,
  input  Read_Select_2,
  input  Write_Select,
  input  [2:0] Write_Data,
  input  Clock,
  output [2:0] Read_Data_1,
  output [2:0] Read_Date_2,
  output [2:0] LOG_Data_2_0
);

  _1x1_Static_RAM_Cell u_1x1_static_ram_cell_1 (
    .Read_Data_1(Read_Data_1[0]), .Write_Select(Write_Select), .Read_Data_2(Read_Date_2[0]),
    .Read_Select_2(Read_Select_2), .Write_Data(Write_Data[0]), .Read_Select_1(Read_Select_1), .Clock(Clock),
    .LOG_Data(LOG_Data_2_0[0]));
  _1x1_Static_RAM_Cell u_1x1_static_ram_cell_2 (
    .Read_Data_1(Read_Data_1[1]), .Write_Select(Write_Select), .Read_Data_2(Read_Date_2[1]),
    .Read_Select_2(Read_Select_2), .Write_Data(Write_Data[1]), .Read_Select_1(Read_Select_1), .Clock(Clock),
    .LOG_Data(LOG_Data_2_0[1]));
  _1x1_Static_RAM_Cell u_1x1_static_ram_cell_3 (
    .Read_Data_1(Read_Data_1[2]), .Write_Select(Write_Select), .Read_Data_2(Read_Date_2[2]),
    .Read_Select_2(Read_Select_2), .Write_Data(Write_Data[2]), .Read_Select_1(Read_Select_1), .Clock(Clock),
    .LOG_Data(LOG_Data_2_0[2]));

  // Other names for the same wires on the sheet: LOG_0 = LOG_Data_2_0[0]; LOG_1 = LOG_Data_2_0[1];
  //   LOG_2 = LOG_Data_2_0[2]
endmodule

module _1x13_SRAM (
  input  Read_Select_1,
  input  Read_Select_2,
  input  Write_Select,
  input  Clock,
  input  [12:0] Write_Data,
  output [12:0] Read_Data_1__12_0,
  output [12:0] Read_Data_2__12_0,
  output [12:0] LOG_Data__12_0
);

  _1x3_SRAM u_1x3_sram_1 (
    .Read_Select_2(Read_Select_2), .Read_Select_1(Read_Select_1), .Write_Data(Write_Data[12:10]),
    .Read_Data_1(Read_Data_1__12_0[12:10]), .Read_Date_2(Read_Data_2__12_0[12:10]),
    .Write_Select(Write_Select), .Clock(Clock), .LOG_Data_2_0(LOG_Data__12_0[12:10]));
  _1x3_SRAM u_1x3_sram_2 (
    .Read_Select_2(Read_Select_2), .Read_Select_1(Read_Select_1), .Write_Data(Write_Data[9:7]),
    .Read_Data_1(Read_Data_1__12_0[9:7]), .Read_Date_2(Read_Data_2__12_0[9:7]), .Write_Select(Write_Select),
    .Clock(Clock), .LOG_Data_2_0(LOG_Data__12_0[9:7]));
  _1x3_SRAM u_1x3_sram_3 (
    .Read_Select_2(Read_Select_2), .Read_Select_1(Read_Select_1), .Write_Data(Write_Data[6:4]),
    .Read_Data_1(Read_Data_1__12_0[6:4]), .Read_Date_2(Read_Data_2__12_0[6:4]), .Write_Select(Write_Select),
    .Clock(Clock), .LOG_Data_2_0(LOG_Data__12_0[6:4]));
  _1x3_SRAM u_1x3_sram_4 (
    .Read_Select_2(Read_Select_2), .Read_Select_1(Read_Select_1), .Write_Data(Write_Data[3:1]),
    .Read_Data_1(Read_Data_1__12_0[3:1]), .Read_Date_2(Read_Data_2__12_0[3:1]), .Write_Select(Write_Select),
    .Clock(Clock), .LOG_Data_2_0(LOG_Data__12_0[3:1]));
  _1x1_Static_RAM_Cell u_1x1_static_ram_cell_1 (
    .Read_Data_1(Read_Data_1__12_0[0]), .Write_Select(Write_Select), .Read_Data_2(Read_Data_2__12_0[0]),
    .Read_Select_2(Read_Select_2), .Write_Data(Write_Data[0]), .Read_Select_1(Read_Select_1), .Clock(Clock),
    .LOG_Data(LOG_Data__12_0[0]));

  // Other names for the same wires on the sheet: LOG_4 = LOG_Data__12_0[0]; LOG_3[2:0] = LOG_Data__12_0[3:1];
  //   LOG_2[2:0] = LOG_Data__12_0[6:4]; LOG_1[2:0] = LOG_Data__12_0[9:7]; LOG_0[2:0] = LOG_Data__12_0[12:10]

  // Notes on the sheet:
  //   Write_Data: pull=down
endmodule

module _4x13_SRAM (
  input  [12:0] Write_Data__12_0,
  input  Write_Enable,
  input  [1:0] Write_Address__1_0,
  input  Read_Address1_Enable,
  input  [1:0] Read_Address_1__1_0,
  input  Read_Address2_Enable,
  input  [1:0] Read_Address_2__1_0,
  input  Clock,
  output [12:0] Read_Data_1__12_0,
  output [12:0] Read_Data_2__12_0,
  output [25:0] LOG_A0_A1__25_0,
  output [25:0] LOG_A2_A3__25_0
);

  wire R1_0, R1_1, R1_2, R1_3, R2_0, R2_0_t, R2_1, R2_1_t, R2_2, R2_3, W0, W1, W2, W3;
  wire [12:0] RD1_0, RD1_1, RD1_2, RD1_3, RD2_0, RD2_1, RD2_2, RD2_3;

  Decoder #(.select(2), .disabled(0)) decoder_1 (
    .out0(W0), .out1(W1), .out2(W2), .out3(W3), .sel(Write_Address__1_0), .en(Write_Enable));
  Decoder #(.select(2), .disabled(0)) decoder_2 (
    .out0(R1_0), .out1(R1_1), .out2(R1_2), .out3(R1_3), .sel(Read_Address_1__1_0), .en(Read_Address1_Enable));
  Decoder #(.select(2), .disabled(0)) decoder_3 (
    .out0(R2_0_t), .out1(R2_1_t), .out2(R2_2), .out3(R2_3), .sel(Read_Address_2__1_0),
    .en(Read_Address2_Enable));
  _1x13_SRAM u_1x13_sram_1 (
    .Read_Select_2(R2_0), .Read_Select_1(R1_0), .Write_Select(W0), .Write_Data(Write_Data__12_0),
    .Read_Data_1__12_0(RD1_0), .Read_Data_2__12_0(RD2_0), .Clock(Clock),
    .LOG_Data__12_0(LOG_A0_A1__25_0[25:13]));
  _1x13_SRAM u_1x13_sram_2 (
    .Read_Select_2(R2_1), .Read_Select_1(R1_1), .Write_Select(W1), .Write_Data(Write_Data__12_0),
    .Read_Data_1__12_0(RD1_1), .Read_Data_2__12_0(RD2_1), .Clock(Clock),
    .LOG_Data__12_0(LOG_A0_A1__25_0[12:0]));
  _1x13_SRAM u_1x13_sram_3 (
    .Read_Select_2(R2_2), .Read_Select_1(R1_2), .Write_Select(W2), .Write_Data(Write_Data__12_0),
    .Read_Data_1__12_0(RD1_2), .Read_Data_2__12_0(RD2_2), .Clock(Clock),
    .LOG_Data__12_0(LOG_A2_A3__25_0[25:13]));
  _1x13_SRAM u_1x13_sram_4 (
    .Read_Select_2(R2_3), .Read_Select_1(R1_3), .Write_Select(W3), .Write_Data(Write_Data__12_0),
    .Read_Data_1__12_0(RD1_3), .Read_Data_2__12_0(RD2_3), .Clock(Clock),
    .LOG_Data__12_0(LOG_A2_A3__25_0[12:0]));
  assign Read_Data_1__12_0 = RD1_0 | RD1_1 | RD1_2 | RD1_3;  // OR_Gate or_1, 13 bits wide
  assign Read_Data_2__12_0 = RD2_0 | RD2_1 | RD2_2 | RD2_3;  // OR_Gate or_2, 13 bits wide

  // Other names for the same wires on the sheet: LOG_A1[12:0] = LOG_A0_A1__25_0[12:0];
  //   LOG_A0[12:0] = LOG_A0_A1__25_0[25:13]; LOG_A3[12:0] = LOG_A2_A3__25_0[12:0];
  //   LOG_A2[12:0] = LOG_A2_A3__25_0[25:13]
endmodule

module _16x13_SRAM (
  input  [3:0] Read_Address_1__3_0,
  input  [3:0] Read_Address_2__3_0,
  input  Read_Address1_Enable,
  input  Read_Address2_Enable,
  input  [3:0] Write_Address__3_0,
  input  [12:0] Write_Data__12_0,
  input  Write_Enable,
  input  Clock,
  output [12:0] Read_Data_1__12_0,
  output [12:0] Read_Data_2__12_0,
  output [25:0] LOG_A0_A1__25_0,
  output [25:0] LOG_A2_A3__25_0,
  output [25:0] LOG_A4_A5__25_0,
  output [25:0] LOG_A6_A7__25_0,
  output [25:0] LOG_A8_A9__25_0,
  output [25:0] LOG_A10_A11__25_0,
  output [25:0] LOG_A12_A13__25_0,
  output [25:0] LOG_A14_A15__25_0
);

  wire R1_0, R1_1, R1_2, R1_3, R2_0, R2_0_t, R2_1, R2_1_t, R2_2, R2_3, W0, W1, W2, W3;
  wire [12:0] RD1_0, RD1_1, RD1_2, RD1_3, RD2_0, RD2_1, RD2_2, RD2_3;

  Decoder #(.select(2), .disabled(0)) decoder_1 (
    .out0(R1_0), .out1(R1_1), .out2(R1_2), .out3(R1_3), .sel(Read_Address_1__3_0[3:2]),
    .en(Read_Address1_Enable));
  Decoder #(.select(2), .disabled(0)) decoder_2 (
    .out0(R2_0_t), .out1(R2_1_t), .out2(R2_2), .out3(R2_3), .sel(Read_Address_2__3_0[3:2]),
    .en(Read_Address2_Enable));
  Decoder #(.select(2), .disabled(0)) decoder_3 (
    .out0(W0), .out1(W1), .out2(W2), .out3(W3), .sel(Write_Address__3_0[3:2]), .en(Write_Enable));
  _4x13_SRAM u_4x13_sram_1 (
    .Write_Data__12_0(Write_Data__12_0), .Write_Enable(W0), .Write_Address__1_0(Write_Address__3_0[1:0]),
    .Read_Address_1__1_0(Read_Address_1__3_0[1:0]), .Read_Address_2__1_0(Read_Address_2__3_0[1:0]),
    .Read_Data_1__12_0(RD1_0), .Read_Data_2__12_0(RD2_0), .Clock(Clock), .Read_Address1_Enable(R1_0),
    .Read_Address2_Enable(R2_0), .LOG_A0_A1__25_0(LOG_A0_A1__25_0), .LOG_A2_A3__25_0(LOG_A2_A3__25_0));
  _4x13_SRAM u_4x13_sram_2 (
    .Write_Data__12_0(Write_Data__12_0), .Write_Enable(W1), .Write_Address__1_0(Write_Address__3_0[1:0]),
    .Read_Address_1__1_0(Read_Address_1__3_0[1:0]), .Read_Address_2__1_0(Read_Address_2__3_0[1:0]),
    .Read_Data_1__12_0(RD1_1), .Read_Data_2__12_0(RD2_1), .Clock(Clock), .Read_Address1_Enable(R1_1),
    .Read_Address2_Enable(R2_1), .LOG_A0_A1__25_0(LOG_A4_A5__25_0), .LOG_A2_A3__25_0(LOG_A6_A7__25_0));
  _4x13_SRAM u_4x13_sram_3 (
    .Write_Data__12_0(Write_Data__12_0), .Write_Enable(W2), .Write_Address__1_0(Write_Address__3_0[1:0]),
    .Read_Address_1__1_0(Read_Address_1__3_0[1:0]), .Read_Address_2__1_0(Read_Address_2__3_0[1:0]),
    .Read_Data_1__12_0(RD1_2), .Read_Data_2__12_0(RD2_2), .Clock(Clock), .Read_Address1_Enable(R1_2),
    .Read_Address2_Enable(R2_2), .LOG_A0_A1__25_0(LOG_A8_A9__25_0), .LOG_A2_A3__25_0(LOG_A10_A11__25_0));
  _4x13_SRAM u_4x13_sram_4 (
    .Write_Data__12_0(Write_Data__12_0), .Write_Enable(W3), .Write_Address__1_0(Write_Address__3_0[1:0]),
    .Read_Address_1__1_0(Read_Address_1__3_0[1:0]), .Read_Address_2__1_0(Read_Address_2__3_0[1:0]),
    .Read_Data_1__12_0(RD1_3), .Read_Data_2__12_0(RD2_3), .Clock(Clock), .Read_Address1_Enable(R1_3),
    .Read_Address2_Enable(R2_3), .LOG_A0_A1__25_0(LOG_A12_A13__25_0), .LOG_A2_A3__25_0(LOG_A14_A15__25_0));
  assign Read_Data_1__12_0 = RD1_0 | RD1_1 | RD1_2 | RD1_3;  // OR_Gate or_1, 13 bits wide
  assign Read_Data_2__12_0 = RD2_0 | RD2_1 | RD2_2 | RD2_3;  // OR_Gate or_2, 13 bits wide

  // Other names for the same wires on the sheet: LOG_A0_A1[25:0] = LOG_A0_A1__25_0; LOG_A2_A3[25:0] = LOG_A2_A3__25_0;
  //   LOG_A4_A5[25:0] = LOG_A4_A5__25_0; LOG_A6_A7[25:0] = LOG_A6_A7__25_0; LOG_A8_A9[25:0] = LOG_A8_A9__25_0;
  //   LOG_A10_A11[25:0] = LOG_A10_A11__25_0; LOG_A12_A13[25:0] = LOG_A12_A13__25_0;
  //   LOG_A14_A15[25:0] = LOG_A14_A15__25_0; RA1_E = Read_Address1_Enable; RA2_E = Read_Address2_Enable;
  //   RA1_0[1:0] = Read_Address_1__3_0[1:0]; RA1_1[1:0] = Read_Address_1__3_0[3:2];
  //   RA2_0[1:0] = Read_Address_2__3_0[1:0]; RA2_1[1:0] = Read_Address_2__3_0[3:2]; WD[12:0] = Write_Data__12_0;
  //   WE = Write_Enable; WA0[1:0] = Write_Address__3_0[1:0]; WA1[1:0] = Write_Address__3_0[3:2]
endmodule

module _64x13_SRAM (
  input  [5:0] Read_Address_1__5_0,
  input  [5:0] Read_Address_2__5_0,
  input  Read_Address1_Enable,
  input  Read_Address2_Enable,
  input  [5:0] Write_Address__5_0,
  input  [12:0] Write_Data__12_0,
  input  Write_Enable,
  input  Clock,
  input  [1:0] LOG_Sel_1_0,
  output [12:0] Read_Data_1__12_0,
  output [12:0] Read_Data_2__12_0,
  output [25:0] LOG_A0_A1__25_0,
  output [25:0] LOG_A2_A3__25_0,
  output [25:0] LOG_A4_A5__25_0,
  output [25:0] LOG_A6_A7__25_0,
  output [25:0] LOG_A8_A9__25_0,
  output [25:0] LOG_A10_A11__25_0,
  output [25:0] LOG_A12_A13__25_0,
  output [25:0] LOG_A14_A15__25_0
);

  wire R1_0, R1_1, R1_2, R1_3, R2_0, R2_0_t, R2_1, R2_1_t, R2_2, R2_3, W0, W1, W2, W3;
  wire [12:0] RD1_0, RD1_1, RD1_2, RD1_3, RD2_0, RD2_1, RD2_2, RD2_3;
  wire [25:0] LOG_A0_A1, LOG_A2_A3, LOG_A4_A5, LOG_A6_A7, LOG_A8_A9, LOG_A10_A11, LOG_A12_A13, LOG_A14_A15,
       LOG_A16_A17, LOG_A18_A19, LOG_A20_A21, LOG_A22_A23, LOG_A24_A25, LOG_A26_A27, LOG_A28_A29,
       LOG_A30_A31, LOG_A32_A33, LOG_A34_A35, LOG_A36_A37, LOG_A38_A39, LOG_A40_A41, LOG_A42_A43,
       LOG_A44_A45, LOG_A46_A47, LOG_A48_A49, LOG_A50_A51, LOG_A52_A53, LOG_A54_A55, LOG_A56_A57,
       LOG_A58_A59, LOG_A60_A61, LOG_A62_A63;

  Decoder #(.select(2), .disabled(0)) decoder_1 (
    .out0(R1_0), .out1(R1_1), .out2(R1_2), .out3(R1_3), .sel(Read_Address_1__5_0[5:4]),
    .en(Read_Address1_Enable));
  Decoder #(.select(2), .disabled(0)) decoder_2 (
    .out0(R2_0_t), .out1(R2_1_t), .out2(R2_2), .out3(R2_3), .sel(Read_Address_2__5_0[5:4]),
    .en(Read_Address2_Enable));
  Decoder #(.select(2), .disabled(0)) decoder_3 (
    .out0(W0), .out1(W1), .out2(W2), .out3(W3), .sel(Write_Address__5_0[5:4]), .en(Write_Enable));
  _16x13_SRAM u_16x13_sram_1 (
    .Write_Data__12_0(Write_Data__12_0), .Write_Enable(W2), .Read_Address1_Enable(R1_2),
    .Read_Address2_Enable(R2_2), .Write_Address__3_0(Write_Address__5_0[3:0]),
    .Read_Address_1__3_0(Read_Address_1__5_0[3:0]), .Read_Address_2__3_0(Read_Address_2__5_0[3:0]),
    .Read_Data_1__12_0(RD1_2), .Read_Data_2__12_0(RD2_2), .Clock(Clock), .LOG_A0_A1__25_0(LOG_A32_A33),
    .LOG_A2_A3__25_0(LOG_A34_A35), .LOG_A4_A5__25_0(LOG_A36_A37), .LOG_A6_A7__25_0(LOG_A38_A39),
    .LOG_A8_A9__25_0(LOG_A40_A41), .LOG_A10_A11__25_0(LOG_A42_A43), .LOG_A12_A13__25_0(LOG_A44_A45),
    .LOG_A14_A15__25_0(LOG_A46_A47));
  _16x13_SRAM u_16x13_sram_2 (
    .Write_Data__12_0(Write_Data__12_0), .Write_Enable(W0), .Read_Address1_Enable(R1_0),
    .Read_Address2_Enable(R2_0), .Write_Address__3_0(Write_Address__5_0[3:0]),
    .Read_Address_1__3_0(Read_Address_1__5_0[3:0]), .Read_Address_2__3_0(Read_Address_2__5_0[3:0]),
    .Read_Data_1__12_0(RD1_0), .Read_Data_2__12_0(RD2_0), .Clock(Clock), .LOG_A0_A1__25_0(LOG_A0_A1),
    .LOG_A2_A3__25_0(LOG_A2_A3), .LOG_A4_A5__25_0(LOG_A4_A5), .LOG_A6_A7__25_0(LOG_A6_A7),
    .LOG_A8_A9__25_0(LOG_A8_A9), .LOG_A10_A11__25_0(LOG_A10_A11), .LOG_A12_A13__25_0(LOG_A12_A13),
    .LOG_A14_A15__25_0(LOG_A14_A15));
  _16x13_SRAM u_16x13_sram_3 (
    .Write_Data__12_0(Write_Data__12_0), .Write_Enable(W1), .Read_Address1_Enable(R1_1),
    .Read_Address2_Enable(R2_1), .Write_Address__3_0(Write_Address__5_0[3:0]),
    .Read_Address_1__3_0(Read_Address_1__5_0[3:0]), .Read_Address_2__3_0(Read_Address_2__5_0[3:0]),
    .Read_Data_1__12_0(RD1_1), .Read_Data_2__12_0(RD2_1), .Clock(Clock), .LOG_A0_A1__25_0(LOG_A16_A17),
    .LOG_A2_A3__25_0(LOG_A18_A19), .LOG_A4_A5__25_0(LOG_A20_A21), .LOG_A6_A7__25_0(LOG_A22_A23),
    .LOG_A8_A9__25_0(LOG_A24_A25), .LOG_A10_A11__25_0(LOG_A26_A27), .LOG_A12_A13__25_0(LOG_A28_A29),
    .LOG_A14_A15__25_0(LOG_A30_A31));
  _16x13_SRAM u_16x13_sram_4 (
    .Write_Data__12_0(Write_Data__12_0), .Write_Enable(W3), .Read_Address1_Enable(R1_3),
    .Read_Address2_Enable(R2_3), .Write_Address__3_0(Write_Address__5_0[3:0]),
    .Read_Address_1__3_0(Read_Address_1__5_0[3:0]), .Read_Address_2__3_0(Read_Address_2__5_0[3:0]),
    .Read_Data_1__12_0(RD1_3), .Read_Data_2__12_0(RD2_3), .Clock(Clock), .LOG_A0_A1__25_0(LOG_A48_A49),
    .LOG_A2_A3__25_0(LOG_A50_A51), .LOG_A4_A5__25_0(LOG_A52_A53), .LOG_A6_A7__25_0(LOG_A54_A55),
    .LOG_A8_A9__25_0(LOG_A56_A57), .LOG_A10_A11__25_0(LOG_A58_A59), .LOG_A12_A13__25_0(LOG_A60_A61),
    .LOG_A14_A15__25_0(LOG_A62_A63));
  DotMatrix #(.inputtype("row"), .matrixcols(13), .matrixrows(2), .dotshape("circle")) dotmatrix_1 (
    .row0(LOG_A0_A1[25:13]), .row1(LOG_A0_A1[12:0]));
  DotMatrix #(.inputtype("row"), .matrixcols(13), .matrixrows(2), .dotshape("circle")) dotmatrix_2 (
    .row0(LOG_A2_A3[25:13]), .row1(LOG_A2_A3[12:0]));
  DotMatrix #(.inputtype("row"), .matrixcols(13), .matrixrows(2), .dotshape("circle")) dotmatrix_3 (
    .row0(LOG_A4_A5[25:13]), .row1(LOG_A4_A5[12:0]));
  DotMatrix #(.inputtype("row"), .matrixcols(13), .matrixrows(2), .dotshape("circle")) dotmatrix_4 (
    .row0(LOG_A6_A7[25:13]), .row1(LOG_A6_A7[12:0]));
  DotMatrix #(.inputtype("row"), .matrixcols(13), .matrixrows(2), .dotshape("circle")) dotmatrix_5 (
    .row0(LOG_A8_A9[25:13]), .row1(LOG_A8_A9[12:0]));
  DotMatrix #(.inputtype("row"), .matrixcols(13), .matrixrows(2), .dotshape("circle")) dotmatrix_6 (
    .row0(LOG_A10_A11[25:13]), .row1(LOG_A10_A11[12:0]));
  DotMatrix #(.inputtype("row"), .matrixcols(13), .matrixrows(2), .dotshape("circle")) dotmatrix_7 (
    .row0(LOG_A12_A13[25:13]), .row1(LOG_A12_A13[12:0]));
  DotMatrix #(.inputtype("row"), .matrixcols(13), .matrixrows(2), .dotshape("circle")) dotmatrix_8 (
    .row0(LOG_A14_A15[25:13]), .row1(LOG_A14_A15[12:0]));
  DotMatrix #(.inputtype("row"), .matrixcols(13), .matrixrows(2), .dotshape("circle")) dotmatrix_9 (
    .row0(LOG_A16_A17[25:13]), .row1(LOG_A16_A17[12:0]));
  DotMatrix #(.inputtype("row"), .matrixcols(13), .matrixrows(2), .dotshape("circle")) dotmatrix_10 (
    .row0(LOG_A18_A19[25:13]), .row1(LOG_A18_A19[12:0]));
  DotMatrix #(.inputtype("row"), .matrixcols(13), .matrixrows(2), .dotshape("circle")) dotmatrix_11 (
    .row0(LOG_A20_A21[25:13]), .row1(LOG_A20_A21[12:0]));
  DotMatrix #(.inputtype("row"), .matrixcols(13), .matrixrows(2), .dotshape("circle")) dotmatrix_12 (
    .row0(LOG_A22_A23[25:13]), .row1(LOG_A22_A23[12:0]));
  DotMatrix #(.inputtype("row"), .matrixcols(13), .matrixrows(2), .dotshape("circle")) dotmatrix_13 (
    .row0(LOG_A24_A25[25:13]), .row1(LOG_A24_A25[12:0]));
  DotMatrix #(.inputtype("row"), .matrixcols(13), .matrixrows(2), .dotshape("circle")) dotmatrix_14 (
    .row0(LOG_A26_A27[25:13]), .row1(LOG_A26_A27[12:0]));
  DotMatrix #(.inputtype("row"), .matrixcols(13), .matrixrows(2), .dotshape("circle")) dotmatrix_15 (
    .row0(LOG_A28_A29[25:13]), .row1(LOG_A28_A29[12:0]));
  DotMatrix #(.inputtype("row"), .matrixcols(13), .matrixrows(2), .dotshape("circle")) dotmatrix_16 (
    .row0(LOG_A30_A31[25:13]), .row1(LOG_A30_A31[12:0]));
  DotMatrix #(.inputtype("row"), .matrixcols(13), .matrixrows(2), .dotshape("circle")) dotmatrix_17 (
    .row0(LOG_A32_A33[25:13]), .row1(LOG_A32_A33[12:0]));
  DotMatrix #(.inputtype("row"), .matrixcols(13), .matrixrows(2), .dotshape("circle")) dotmatrix_18 (
    .row0(LOG_A34_A35[25:13]), .row1(LOG_A34_A35[12:0]));
  DotMatrix #(.inputtype("row"), .matrixcols(13), .matrixrows(2), .dotshape("circle")) dotmatrix_19 (
    .row0(LOG_A36_A37[25:13]), .row1(LOG_A36_A37[12:0]));
  DotMatrix #(.inputtype("row"), .matrixcols(13), .matrixrows(2), .dotshape("circle")) dotmatrix_20 (
    .row0(LOG_A38_A39[25:13]), .row1(LOG_A38_A39[12:0]));
  DotMatrix #(.inputtype("row"), .matrixcols(13), .matrixrows(2), .dotshape("circle")) dotmatrix_21 (
    .row0(LOG_A40_A41[25:13]), .row1(LOG_A40_A41[12:0]));
  DotMatrix #(.inputtype("row"), .matrixcols(13), .matrixrows(2), .dotshape("circle")) dotmatrix_22 (
    .row0(LOG_A42_A43[25:13]), .row1(LOG_A42_A43[12:0]));
  DotMatrix #(.inputtype("row"), .matrixcols(13), .matrixrows(2), .dotshape("circle")) dotmatrix_23 (
    .row0(LOG_A44_A45[25:13]), .row1(LOG_A44_A45[12:0]));
  DotMatrix #(.inputtype("row"), .matrixcols(13), .matrixrows(2), .dotshape("circle")) dotmatrix_24 (
    .row0(LOG_A46_A47[25:13]), .row1(LOG_A46_A47[12:0]));
  DotMatrix #(.inputtype("row"), .matrixcols(13), .matrixrows(2), .dotshape("circle")) dotmatrix_25 (
    .row0(LOG_A48_A49[25:13]), .row1(LOG_A48_A49[12:0]));
  DotMatrix #(.inputtype("row"), .matrixcols(13), .matrixrows(2), .dotshape("circle")) dotmatrix_26 (
    .row0(LOG_A50_A51[25:13]), .row1(LOG_A50_A51[12:0]));
  DotMatrix #(.inputtype("row"), .matrixcols(13), .matrixrows(2), .dotshape("circle")) dotmatrix_27 (
    .row0(LOG_A52_A53[25:13]), .row1(LOG_A52_A53[12:0]));
  DotMatrix #(.inputtype("row"), .matrixcols(13), .matrixrows(2), .dotshape("circle")) dotmatrix_28 (
    .row0(LOG_A54_A55[25:13]), .row1(LOG_A54_A55[12:0]));
  DotMatrix #(.inputtype("row"), .matrixcols(13), .matrixrows(2), .dotshape("circle")) dotmatrix_29 (
    .row0(LOG_A56_A57[25:13]), .row1(LOG_A56_A57[12:0]));
  DotMatrix #(.inputtype("row"), .matrixcols(13), .matrixrows(2), .dotshape("circle")) dotmatrix_30 (
    .row0(LOG_A58_A59[25:13]), .row1(LOG_A58_A59[12:0]));
  DotMatrix #(.inputtype("row"), .matrixcols(13), .matrixrows(2), .dotshape("circle")) dotmatrix_31 (
    .row0(LOG_A60_A61[25:13]), .row1(LOG_A60_A61[12:0]));
  DotMatrix #(.inputtype("row"), .matrixcols(13), .matrixrows(2), .dotshape("circle")) dotmatrix_32 (
    .row0(LOG_A62_A63[25:13]), .row1(LOG_A62_A63[12:0]));
  assign Read_Data_1__12_0 = RD1_0 | RD1_1 | RD1_2 | RD1_3;  // OR_Gate or_1, 13 bits wide
  assign Read_Data_2__12_0 = RD2_0 | RD2_1 | RD2_2 | RD2_3;  // OR_Gate or_2, 13 bits wide
  Multiplexer #(.select(2), .width(26), .disabled(0), .enable("false")) multiplexer_1 (
    .in0(LOG_A0_A1), .in1(LOG_A16_A17), .in2(LOG_A32_A33), .in3(LOG_A48_A49), .out(LOG_A0_A1__25_0),
    .sel(LOG_Sel_1_0));
  Multiplexer #(.select(2), .width(26), .disabled(0), .enable("false")) multiplexer_2 (
    .in0(LOG_A2_A3), .in1(LOG_A18_A19), .in2(LOG_A34_A35), .in3(LOG_A50_A51), .out(LOG_A2_A3__25_0),
    .sel(LOG_Sel_1_0));
  Multiplexer #(.select(2), .width(26), .disabled(0), .enable("false")) multiplexer_3 (
    .in0(LOG_A4_A5), .in1(LOG_A20_A21), .in2(LOG_A36_A37), .in3(LOG_A52_A53), .out(LOG_A4_A5__25_0),
    .sel(LOG_Sel_1_0));
  Multiplexer #(.select(2), .width(26), .disabled(0), .enable("false")) multiplexer_4 (
    .in0(LOG_A6_A7), .in1(LOG_A22_A23), .in2(LOG_A38_A39), .in3(LOG_A54_A55), .out(LOG_A6_A7__25_0),
    .sel(LOG_Sel_1_0));
  Multiplexer #(.select(2), .width(26), .disabled(0), .enable("false")) multiplexer_5 (
    .in0(LOG_A8_A9), .in1(LOG_A26_A27), .in2(LOG_A42_A43), .in3(LOG_A58_A59), .out(LOG_A8_A9__25_0),
    .sel(LOG_Sel_1_0));
  Multiplexer #(.select(2), .width(26), .disabled(0), .enable("false")) multiplexer_6 (
    .in0(LOG_A10_A11), .in1(LOG_A26_A27), .in2(LOG_A42_A43), .in3(LOG_A58_A59), .out(LOG_A10_A11__25_0),
    .sel(LOG_Sel_1_0));
  Multiplexer #(.select(2), .width(26), .disabled(0), .enable("false")) multiplexer_7 (
    .in0(LOG_A12_A13), .in1(LOG_A28_A29), .in2(LOG_A44_A45), .in3(LOG_A60_A61), .out(LOG_A12_A13__25_0),
    .sel(LOG_Sel_1_0));
  Multiplexer #(.select(2), .width(26), .disabled(0), .enable("false")) multiplexer_8 (
    .in0(LOG_A14_A15), .in1(LOG_A30_A31), .in2(LOG_A46_A47), .in3(LOG_A62_A63), .out(LOG_A14_A15__25_0),
    .sel(LOG_Sel_1_0));

  // Other names for the same wires on the sheet: RA1_E = Read_Address1_Enable; RA2_E = Read_Address2_Enable;
  //   RA1_0[3:0] = Read_Address_1__5_0[3:0]; RA1_1[1:0] = Read_Address_1__5_0[5:4];
  //   RA2_0[3:0] = Read_Address_2__5_0[3:0]; RA2_1[1:0] = Read_Address_2__5_0[5:4]; WD[12:0] = Write_Data__12_0;
  //   WE = Write_Enable; WA0[3:0] = Write_Address__5_0[3:0]; WA1[1:0] = Write_Address__5_0[5:4]

  // Notes on the sheet:
  //   A0+A1
  //   A2+A3
  //   A4+A5
  //   A6+A7
  //   A8+A9
  //   A10+A11
  //   A12+A13
  //   A14+A15
  //   A16+A17
  //   A18+A19
  //   A20+A21
  //   A22+A23
  //   A24+A25
  //   A26+A27
  //   A28+A29
  //   A30+A31
  //   A32+A33
  //   A34+A35
  //   A36+A37
  //   A38+A39
  //   A40+A41
  //   A42+A43
  //   A44+A45
  //   A46+A47
  //   A48+A49
  //   A50+A51
  //   A52+A53
  //   A54+A55
  //   A56+A57
  //   A58+A59
  //   A60+A61
  //   A62+A63
endmodule

module _128X13_SRAM (
  input  [6:0] Read_Address_1__6_0,
  input  [6:0] Read_Address_2__6_0,
  input  [6:0] Write_Address__6_0,
  input  [12:0] Write_Data__12_0,
  input  Write_Enable,
  input  Clock,
  input  [2:0] LOG_Sel_2_0,
  output [25:0] _0,
  output [25:0] _2,
  output [25:0] _4,
  output [25:0] _6,
  output [12:0] Read_Data_1__12_0,
  output [25:0] _8,
  output [12:0] Read_Data_2__12_0,
  output [25:0] _10,
  output [25:0] _12,
  output [25:0] _14
);

  wire R1_0, R1_1, R2_0, R2_1, W0, W1;
  wire [12:0] RD1_0, RD1_1, RD2_0, RD2_1;
  wire [25:0] A0, A2, A4, A6, A8, A10, A12, A14, B0, B2, B4, B6, B8, B10, B12, B14;

  Decoder #(.disabled(0), .enable("false")) decoder_1 (.out0(R1_0), .out1(R1_1), .sel(Read_Address_1__6_0[6]));
  Decoder #(.disabled(0), .enable("false")) decoder_2 (.out0(R2_0), .out1(R2_1), .sel(Read_Address_2__6_0[6]));
  Decoder #(.disabled(0)) decoder_3 (.out0(W0), .out1(W1), .sel(Write_Address__6_0[6]), .en(Write_Enable));
  _64x13_SRAM u_64x13_sram_1 (
    .Read_Address_1__5_0(Read_Address_1__6_0[5:0]), .Read_Address_2__5_0(Read_Address_2__6_0[5:0]),
    .Write_Address__5_0(Write_Address__6_0[5:0]), .Write_Data__12_0(Write_Data__12_0), .Write_Enable(W0),
    .Clock(Clock), .Read_Data_1__12_0(RD1_0), .Read_Data_2__12_0(RD2_0), .LOG_A0_A1__25_0(A0),
    .LOG_A2_A3__25_0(A2), .LOG_A4_A5__25_0(A4), .LOG_A6_A7__25_0(A6), .LOG_A8_A9__25_0(A8),
    .LOG_A10_A11__25_0(A10), .LOG_A12_A13__25_0(A12), .LOG_A14_A15__25_0(A14),
    .LOG_Sel_1_0(LOG_Sel_2_0[1:0]), .Read_Address1_Enable(R1_0), .Read_Address2_Enable(R2_0));
  _64x13_SRAM u_64x13_sram_2 (
    .Read_Address_1__5_0(Read_Address_1__6_0[5:0]), .Read_Address_2__5_0(Read_Address_2__6_0[5:0]),
    .Write_Address__5_0(Write_Address__6_0[5:0]), .Write_Data__12_0(Write_Data__12_0), .Write_Enable(W1),
    .Clock(Clock), .Read_Data_1__12_0(RD1_1), .Read_Data_2__12_0(RD2_1), .LOG_A0_A1__25_0(B0),
    .LOG_A2_A3__25_0(B2), .LOG_A4_A5__25_0(B4), .LOG_A6_A7__25_0(B6), .LOG_A8_A9__25_0(B8),
    .LOG_A10_A11__25_0(B10), .LOG_A12_A13__25_0(B12), .LOG_A14_A15__25_0(B14),
    .LOG_Sel_1_0(LOG_Sel_2_0[1:0]), .Read_Address1_Enable(R1_1), .Read_Address2_Enable(R2_1));
  assign Read_Data_1__12_0 = RD1_0 | RD1_1;  // OR_Gate or_1, 13 bits wide
  assign Read_Data_2__12_0 = RD2_0 | RD2_1;  // OR_Gate or_2, 13 bits wide
  Multiplexer #(.width(26), .disabled(0), .enable("false")) multiplexer_1 (
    .in0(A0), .in1(B0), .out(_0), .sel(LOG_Sel_2_0[2]));
  Multiplexer #(.width(26), .disabled(0), .enable("false")) multiplexer_2 (
    .in0(A2), .in1(B2), .out(_2), .sel(LOG_Sel_2_0[2]));
  Multiplexer #(.width(26), .disabled(0), .enable("false")) multiplexer_3 (
    .in0(A4), .in1(B4), .out(_4), .sel(LOG_Sel_2_0[2]));
  Multiplexer #(.width(26), .disabled(0), .enable("false")) multiplexer_4 (
    .in0(A6), .in1(B6), .out(_6), .sel(LOG_Sel_2_0[2]));
  Multiplexer #(.width(26), .disabled(0), .enable("false")) multiplexer_5 (
    .in0(A8), .in1(B8), .out(_8), .sel(LOG_Sel_2_0[2]));
  Multiplexer #(.width(26), .disabled(0), .enable("false")) multiplexer_6 (
    .in0(A10), .in1(B10), .out(_10), .sel(LOG_Sel_2_0[2]));
  Multiplexer #(.width(26), .disabled(0), .enable("false")) multiplexer_7 (
    .in0(A12), .in1(B12), .out(_12), .sel(LOG_Sel_2_0[2]));
  Multiplexer #(.width(26), .disabled(0), .enable("false")) multiplexer_8 (
    .in0(A14), .in1(B14), .out(_14), .sel(LOG_Sel_2_0[2]));

  // Other names for the same wires on the sheet: LOG_Sel_1_0[1:0] = LOG_Sel_2_0[1:0]; LOG_Sel = LOG_Sel_2_0[2];
  //   RA1_0[5:0] = Read_Address_1__6_0[5:0]; RA1_1 = Read_Address_1__6_0[6]; RA2_0[5:0] = Read_Address_2__6_0[5:0];
  //   RA2_1 = Read_Address_2__6_0[6]; WD[12:0] = Write_Data__12_0; WE = Write_Enable;
  //   WA0[5:0] = Write_Address__6_0[5:0]; WA1 = Write_Address__6_0[6]
endmodule

module MAIN (
  input  [6:0] Read_Address_1__6_0,
  input  [6:0] Read_Address_2__6_0,
  input  [6:0] Write_Address__6_0,
  input  [12:0] Write_Data__12_0,
  input  Write_Enable,
  input  Clock,
  input  [2:0] LOG_Sel_2_0,
  output [12:0] Read_Data_1__12_0,
  output [12:0] Read_Data_2__12_0
);

  wire [25:0] A0, A2, A4, A6, A8, A10, A12, A14;

  DotMatrix #(.inputtype("row"), .matrixcols(13), .matrixrows(2), .dotshape("circle")) dotmatrix_1 (
    .row0(A0[25:13]), .row1(A0[12:0]));
  DotMatrix #(.inputtype("row"), .matrixcols(13), .matrixrows(2), .dotshape("circle")) dotmatrix_2 (
    .row0(A2[25:13]), .row1(A2[12:0]));
  DotMatrix #(.inputtype("row"), .matrixcols(13), .matrixrows(2), .dotshape("circle")) dotmatrix_3 (
    .row0(A4[25:13]), .row1(A4[12:0]));
  DotMatrix #(.inputtype("row"), .matrixcols(13), .matrixrows(2), .dotshape("circle")) dotmatrix_4 (
    .row0(A6[25:13]), .row1(A6[12:0]));
  DotMatrix #(.inputtype("row"), .matrixcols(13), .matrixrows(2), .dotshape("circle")) dotmatrix_5 (
    .row0(A8[25:13]), .row1(A8[12:0]));
  DotMatrix #(.inputtype("row"), .matrixcols(13), .matrixrows(2), .dotshape("circle")) dotmatrix_6 (
    .row0(A10[25:13]), .row1(A10[12:0]));
  DotMatrix #(.inputtype("row"), .matrixcols(13), .matrixrows(2), .dotshape("circle")) dotmatrix_7 (
    .row0(A12[25:13]), .row1(A12[12:0]));
  DotMatrix #(.inputtype("row"), .matrixcols(13), .matrixrows(2), .dotshape("circle")) dotmatrix_8 (
    .row0(A14[25:13]), .row1(A14[12:0]));
  // _128X13_SRAM 128x13_sram_1: pin names not known; wires that end beside it: Read_Address_1__6_0, Read_Address_2__6_0, Write_Address__6_0, Write_Data__12_0, Write_Enable, Clock, Read_Data_1__12_0, Read_Data_2__12_0

  // Notes on the sheet:
  //   A0+A1
  //   A2+A3
  //   A4+A5
  //   A6+A7
  //   A8+A9
  //   A10+A11
  //   A12+A13
  //   A14+A15
endmodule
